// Logisim project Branch Control.circ as structural Verilog
module Branch_Control (
  input  [31:0] in_1,
  input  [31:0] in_2,
  input  [31:0] in_3,
  input  [1:0] Operacion,
  output [31:0] out_5
);

  wire [31:0] Ix4, PC_4, PC_4_4xI;

  Adder #(.width(32)) adder_1 (.a(in_1), .b(32'h4), .out(PC_4));  // open: cin, cout
  Multiplier #(.width(32)) multiplier_1 (.a(in_2), .b(32'h4), .out(Ix4));  // open: cin, cout
  Adder #(.width(32)) adder_2 (.a(PC_4), .b(Ix4), .out(PC_4_4xI));  // open: cin, cout
  Multiplexer #(.select(2), .width(32), .enable("false")) multiplexer_1 (
    .in0(PC_4), .in1(PC_4_4xI), .in2({in_1[31:28], in_2[25:0], 2'b00}), .in3(in_3), .out(out_5),
    .sel(Operacion));

  // Other names for the same wires on the sheet: I[31:0] = in_2; PC[31:0] = in_1; I25__0[25:0] = in_2[25:0];
  //   PC__I__0[31:2] = {in_1[31:28], in_2[25:0]}; PC31__28[3:0] = in_1[31:28]; RS[31:0] = in_3

  // Notes on the sheet:
  //   in_1: pull=down
  //   out_5: pull=down
  //   RS
  //   Entradas
  //   PC
  //   Offset
  //   Branch Control
  //   Operaciones
  //   Normal
  //   Multiplicacion
  //   Concatenacion
  //   Para las Operaciones
  //   00 PC+4
  //   01 PC+4+4*offset
  //   10 PC||I||0^2
  //   11 RS
  //   Proximo valor de PC
  //   Salida [PC]
endmodule

module Program_Counter (
  input  [31:0] PC,
  input  Load,
  input  Reset,
  input  Reloj,
  output [31:0] out_5
);

  Register #(.width(32)) Program_Counter (.D(PC), .en(Load), .Q(out_5), .clk(Reloj), .clr(Reset));

  // Other names for the same wires on the sheet: CLK = Reloj; PC_t[31:0] = out_5

  // Notes on the sheet:
  //   Load
endmodule
