// Logisim project CACHE-Unit.circ as structural Verilog: 2 circuits, main circuit Contador de Ciclos
module Contador_de_Ciclos (
  input  [3:0] Read_Time,
  input  [3:0] Write_Time,
  input  Reloj,
  input  R_W,
  input  in_5,
  input  in_6,
  output WAIT
);

  wire [3:0] counter_1_q, RT__WT;

  Multiplexer #(.width(4), .enable("false")) multiplexer_1 (.in0(Read_Time), .in1(Write_Time), .out(RT__WT), .sel(R_W));
  Counter #(.width(4), .max('hf)) counter_1 (
    .count(in_5), .Q(counter_1_q), .clk(Reloj), .clr(in_6));  // open: load, D, carry
  Comparator #(.width(4)) comparator_1 (.a(counter_1_q), .b(RT__WT), .eq(WAIT));  // open: gt, lt

  // Other names for the same wires on the sheet: CLK = Reloj; CS = in_5; RST = in_6

  // Notes on the sheet:
  //   Entradas de Tiempo
  //   Contador de Ciclos del Reloj
endmodule

module CACHE_UNIT (
  input  in_1,
  input  RST,
  input  in_3,
  input  rw,
  input  [3:0] in_5,
  input  [3:0] in_6,
  input  in_7,
  input  in_8,
  input  [31:0] ADRESS,
  input  LOADADRESS,
  input  [31:0] in_11,
  input  in_12,
  input  [31:0] in_13,
  input  [31:0] in_14,
  input  [31:0] in_15,
  output out_16,
  output FINISH,
  output [31:0] out_18,
  output [15:0] RAMADRESS,
  output CHIFT_SELECT,
  output [31:0] out_21,
  output [31:0] out_22,
  output [31:0] out_23,
  output RW_RAM,
  output [31:0] out_25,
  output [31:0] out_26
);

  wire and_1_out, CLEAN, CS1, CS2, CS3, CS4, CS5, CS7, CS8, D, D1, D2, D3, d_ff_1_q, d_ff_9_q,
       demultiplexer_1_out0, demultiplexer_1_out1, demultiplexer_2_out0, demultiplexer_2_out1,
       demultiplexer_3_out0, demultiplexer_3_out1, demultiplexer_4_out0, demultiplexer_5_out0,
       demultiplexer_5_out1, demultiplexer_6_out0, demultiplexer_6_out1, demultiplexer_7_out0,
       demultiplexer_8_out0, demultiplexer_9_out0, demultiplexer_9_out1, demultiplexer_10_out0,
       demultiplexer_10_out1, DIRTY, F1, HINT, LINEA, not_1_out, or_1_out, or_2_out, or_3_out, or_6_out,
       or_10_out, or_11_out, RW_t, VALIDO, WAIT;

  and and_1 (and_1_out, ~in_7, ~RST);  // AND_Gate
  D_Flip_Flop #(.trigger("falling")) d_ff_1 (
    .clk(in_3), .D(demultiplexer_1_out0), .Q(d_ff_1_q), .preset(and_1_out), .reset(RST));  // open: Qn, en
  Demultiplexer demultiplexer_1 (
    .out0(demultiplexer_1_out0), .out1(demultiplexer_1_out1), .in(d_ff_1_q), .sel(in_7));  // open: en
  not not_1 (not_1_out, CHIFT_SELECT);
  Contador_de_Ciclos contador_de_ciclos_1 (
    .Read_Time(in_5), .Write_Time(in_6), .Reloj(in_3), .R_W(rw), .in_5(CHIFT_SELECT), .in_6(not_1_out),
    .WAIT(WAIT));
  CACHE cache_1 (
    .Adress(ADRESS), .in_4(in_11), .in_5(in_13), .in_6(in_14), .in_7(in_15), .Rst(RST), .OUT(out_22),
    .O1(out_18), .O2(out_21), .O2_2(out_23), .O4(out_25), .HINT(HINT), .DIRTY_2(DIRTY), .CLK(in_3),
    .DIRTY(D), .valid(VALIDO), .RAMADRESS(RAMADRESS), .CLEAN(CLEAN), .finishcacheline(out_16),
    .LoadAdress(LOADADRESS), .RW(RW_t), .LINEA(LINEA), .in_9(in_12), .data(out_26), .RST_OUT(in_8));
  Demultiplexer demultiplexer_2 (
    .out0(demultiplexer_2_out0), .out1(demultiplexer_2_out1), .in(demultiplexer_1_out1), .sel(rw));  // open: en
  Demultiplexer demultiplexer_3 (
    .out0(demultiplexer_3_out0), .out1(demultiplexer_3_out1), .in(demultiplexer_2_out1), .sel(HINT));  // open: en
  Demultiplexer demultiplexer_4 (
    .out0(demultiplexer_4_out0), .out1(F1), .in(demultiplexer_2_out0), .sel(HINT));  // open: en
  Demultiplexer demultiplexer_5 (
    .out0(demultiplexer_5_out0), .out1(demultiplexer_5_out1), .in(demultiplexer_3_out0), .sel(DIRTY));  // open: en
  D_Flip_Flop #(.trigger("falling")) d_ff_2 (
    .clk(in_3), .D(demultiplexer_3_out1), .Q(D1), .reset(RST));  // open: Qn, preset, en
  Demultiplexer demultiplexer_6 (
    .out0(demultiplexer_6_out0), .out1(demultiplexer_6_out1), .in(demultiplexer_4_out0), .sel(DIRTY));  // open: en
  or or_1 (or_1_out, demultiplexer_7_out0, demultiplexer_5_out1);
  or or_2 (or_2_out, demultiplexer_9_out0, demultiplexer_6_out0);
  or or_3 (or_3_out, demultiplexer_6_out1, demultiplexer_8_out0);
  D_Flip_Flop #(.trigger("falling")) d_ff_3 (
    .clk(in_3), .D(or_1_out), .Q(CS4), .en(in_1), .reset(RST));  // open: Qn, preset
  D_Flip_Flop #(.trigger("falling")) d_ff_4 (
    .clk(in_3), .D(or_3_out), .Q(CS2), .en(in_1), .reset(RST));  // open: Qn, preset
  Demultiplexer demultiplexer_7 (.out0(demultiplexer_7_out0), .out1(CS8), .in(CS4), .sel(WAIT));  // open: en
  D_Flip_Flop #(.trigger("falling")) d_ff_5 (
    .clk(in_3), .D(or_2_out), .Q(CS1), .en(in_1), .reset(RST));  // open: Qn, preset
  Demultiplexer demultiplexer_8 (.out0(demultiplexer_8_out0), .out1(CLEAN), .in(CS2), .sel(WAIT));  // open: en
  D_Flip_Flop #(.trigger("falling")) d_ff_6 (
    .clk(in_3), .D(demultiplexer_5_out0), .Q(D3), .en(in_1), .reset(RST));  // open: Qn, preset
  Demultiplexer demultiplexer_9 (
    .out0(demultiplexer_9_out0), .out1(demultiplexer_9_out1), .in(CS1), .sel(WAIT));  // open: en
  D_Flip_Flop #(.trigger("falling")) d_ff_7 (.clk(in_3), .D(CS8), .Q(D2), .en(in_1), .reset(RST));  // open: Qn, preset
  D_Flip_Flop #(.trigger("falling")) d_ff_8 (
    .clk(in_3), .D(demultiplexer_9_out1), .Q(CS5), .en(in_1), .reset(RST));  // open: Qn, preset
  D_Flip_Flop #(.trigger("falling")) d_ff_9 (
    .clk(in_3), .D(CLEAN), .Q(d_ff_9_q), .en(in_1), .reset(RST));  // open: Qn, preset
  or or_4 (D, D1, D2, D3);
  or or_5 (RW_RAM, CS2, CS4);
  or or_6 (or_6_out, demultiplexer_10_out0, d_ff_9_q);
  or or_7 (VALIDO, F1, CS5, CS7, D1, D2, D3);
  or or_8 (LINEA, CS5, CS7);
  or or_9 (RW_t, D1, D2, D3, CS5, CS7);
  or or_10 (or_10_out, CS1, CS2, CS3, CS4, CS5, CLEAN);
  or or_11 (or_11_out, CS7, CS8);
  D_Flip_Flop #(.trigger("falling")) d_ff_10 (
    .clk(in_3), .D(or_6_out), .Q(CS3), .en(in_1), .reset(RST));  // open: Qn, preset
  D_Flip_Flop #(.trigger("falling")) END (
    .clk(in_3), .D(VALIDO), .Q(FINISH), .en(in_1), .reset(RST));  // open: Qn, preset
  or or_12 (CHIFT_SELECT, or_10_out, or_11_out);
  Demultiplexer demultiplexer_10 (
    .out0(demultiplexer_10_out0), .out1(demultiplexer_10_out1), .in(CS3), .sel(WAIT));  // open: en
  D_Flip_Flop #(.trigger("falling")) d_ff_11 (
    .clk(in_3), .D(demultiplexer_10_out1), .Q(CS7), .en(in_1), .reset(RST));  // open: Qn, preset

  // Other names for the same wires on the sheet: CARGAROTRALINEA = out_16; CLK = in_3; CS = CHIFT_SELECT; CS6 = CLEAN;
  //   cs_t = in_7; EN = in_1; RO = in_8; RRW1 = CS2; RRW2 = CS4; F4 = D1; RW1 = D1; F5 = D2; RW2 = D2; F6 = D3;
  //   RW3 = D3; F2 = CS5; L1 = CS5; RW4 = CS5; F3 = CS7; L2 = CS7; RW5 = CS7

  // Notes on the sheet:
  //   LEER
  //   HINT
  //   MISS
  //   ESCRIBE ||RESCRIBE DEPENDIENDO  DEL DIRTY 
  //   ESCRIBE DIRECTAMENTE
  //   EESCRIBE  LA INFO ANTIGUA EN  LA RAM 
  //   ESCRIBIR LA LINEA QUE NO ESTA 
  //   LECTURA DE LA INFO DE LA RAM
  //   ESCRIBIR EN LA RAM
  //   ESPERAR CICLO DE CARGA
  //   ESCRIBE LA INFO NUEVA EN LA CACHE 
  //   ESPERAR CICLO DE CARGA
  //   UN TIEMPO PARA UNA CORRECTA ESCRITURA EN LA RAM
  //   CACHE OPERATION
  //   RAM OPERATION
  //   LEER DE LA RAM LA INFO 
  //   ESPERAR CLOCK  PARA CORRECTO GUARDAADO 
endmodule
