// Logisim project Cache.circ as structural Verilog: 2 circuits, main circuit main
// Inst 0
module main (
  input  [31:0] Instruc_0,
  input  [31:0] Instruc_1,
  input  [31:0] Instruc_2,
  input  [31:0] Instruc_3,
  input  [31:0] Addres,
  input  Reloj,
  input  Reset,
  input  R_W_Cach
);

  wire comparator_1_eq, EN7, EN_0, EN_1, EN_2, EN_3, EN_4, EN_5, EN_6, Invalido, Is_in_Cache, is_valid, v0,
       v1, v2, v3, v4, v5, v6, v7, Valido;
  wire [15:0] STAG, tag_0, tag_1, tag_2, tag_3, tag_4, tag_5, tag_6, tag_7;
  wire [31:0] _0ut_0, _0ut_1, _0ut_2, _0ut_3, _0ut_4, _0ut_5, _0ut_6, _0ut_7, _0ut_8, _0ut_9, _0ut_10,
       _0ut_11, _0ut_12, _0ut_13, _0ut_14, _0ut_15, _0ut_16, _0ut_17, _0ut_18, _0ut_19, _0ut_20, _0ut_21,
       _0ut_22, _0ut_23, _0ut_24, _0ut_25, _0ut_26, _0ut_27, _0ut_28, _0ut_29, _0ut_30, _0ut_31;

  Register #(.width(16)) register_1 (.D(Addres[19:4]), .en(EN_0), .Q(tag_0), .clk(Reloj), .clr(Reset));
  Register #(.width(16)) register_2 (.D(Addres[19:4]), .en(EN_1), .Q(tag_1), .clk(Reloj), .clr(Reset));
  Register #(.width(16)) register_3 (.D(Addres[19:4]), .en(EN_2), .Q(tag_2), .clk(Reloj), .clr(Reset));
  Register #(.width(16)) register_4 (.D(Addres[19:4]), .en(EN_3), .Q(tag_3), .clk(Reloj), .clr(Reset));
  Register #(.width(16)) register_5 (.D(Addres[19:4]), .en(EN_4), .Q(tag_4), .clk(Reloj), .clr(Reset));
  Register #(.width(16)) register_6 (.D(Addres[19:4]), .en(EN_5), .Q(tag_5), .clk(Reloj), .clr(Reset));
  Register #(.width(16)) register_7 (.D(Addres[19:4]), .en(EN_6), .Q(tag_6), .clk(Reloj), .clr(Reset));
  Register #(.width(16)) register_8 (.D(Addres[19:4]), .en(EN7), .Q(tag_7), .clk(Reloj), .clr(Reset));
  Register #(.width(32)) register_9 (.D(Instruc_0), .en(EN_0), .Q(_0ut_0), .clk(Reloj), .clr(Reset));
  Register #(.width(32)) register_10 (.D(Instruc_0), .en(EN_1), .Q(_0ut_4), .clk(Reloj), .clr(Reset));
  Register #(.width(32)) register_11 (.D(Instruc_0), .en(EN_2), .Q(_0ut_8), .clk(Reloj), .clr(Reset));
  Register #(.width(32)) register_12 (.D(Instruc_0), .en(EN_3), .Q(_0ut_12), .clk(Reloj), .clr(Reset));
  Register #(.width(32)) register_13 (.D(Instruc_0), .en(EN_4), .Q(_0ut_16), .clk(Reloj), .clr(Reset));
  Register #(.width(32)) register_14 (.D(Instruc_0), .en(EN_5), .Q(_0ut_20), .clk(Reloj), .clr(Reset));
  Register #(.width(32)) register_15 (.D(Instruc_0), .en(EN_6), .Q(_0ut_24), .clk(Reloj), .clr(Reset));
  Register #(.width(32)) register_16 (.D(Instruc_0), .en(EN7), .Q(_0ut_28), .clk(Reloj), .clr(Reset));
  Decoder #(.select(3), .enable("false")) decoder_1 (
    .out0(EN_0), .out1(EN_1), .out2(EN_2), .out3(EN_3), .out4(EN_4), .out5(EN_5), .out6(EN_6), .out7(EN7),
    .sel(Addres[6:4]));
  Multiplexer #(.select(3), .width(16), .enable("false")) multiplexer_1 (
    .in0(tag_0), .in1(tag_1), .in2(tag_2), .in3(tag_3), .in4(tag_4), .in5(tag_5), .in6(tag_6), .in7(tag_7),
    .out(STAG), .sel(Addres[6:4]));
  Multiplexer #(.select(3), .enable("false")) multiplexer_2 (
    .in0(v0), .in1(v1), .in2(v2), .in3(v3), .in4(v4), .in5(v5), .in6(v6), .in7(v7), .out(is_valid),
    .sel(Addres[6:4]));
  Register #(.width(32)) register_17 (.D(Instruc_1), .en(EN_0), .Q(_0ut_1), .clk(Reloj), .clr(Reset));
  Register #(.width(32)) register_18 (.D(Instruc_1), .en(EN_1), .Q(_0ut_5), .clk(Reloj), .clr(Reset));
  Register #(.width(32)) register_19 (.D(Instruc_1), .en(EN_2), .Q(_0ut_9), .clk(Reloj), .clr(Reset));
  Register #(.width(32)) register_20 (.D(Instruc_1), .en(EN_3), .Q(_0ut_13), .clk(Reloj), .clr(Reset));
  Register #(.width(32)) register_21 (.D(Instruc_1), .en(EN_4), .Q(_0ut_17), .clk(Reloj), .clr(Reset));
  Register #(.width(32)) register_22 (.D(Instruc_1), .en(EN_5), .Q(_0ut_21), .clk(Reloj), .clr(Reset));
  Register #(.width(32)) register_23 (.D(Instruc_1), .en(EN_6), .Q(_0ut_25), .clk(Reloj), .clr(Reset));
  Register #(.width(32)) register_24 (.D(Instruc_1), .en(EN7), .Q(_0ut_29), .clk(Reloj), .clr(Reset));
  Register #(.width(32)) register_25 (.D(Instruc_2), .en(EN_0), .Q(_0ut_2), .clk(Reloj), .clr(Reset));
  Register #(.width(32)) register_26 (.D(Instruc_2), .en(EN_1), .Q(_0ut_6), .clk(Reloj), .clr(Reset));
  Register #(.width(32)) register_27 (.D(Instruc_2), .en(EN_2), .Q(_0ut_10), .clk(Reloj), .clr(Reset));
  Register #(.width(32)) register_28 (.D(Instruc_2), .en(EN_3), .Q(_0ut_14), .clk(Reloj), .clr(Reset));
  Register #(.width(32)) register_29 (.D(Instruc_2), .en(EN_4), .Q(_0ut_18), .clk(Reloj), .clr(Reset));
  Register #(.width(32)) register_30 (.D(Instruc_2), .en(EN_5), .Q(_0ut_22), .clk(Reloj), .clr(Reset));
  Register #(.width(32)) register_31 (.D(Instruc_2), .en(EN_6), .Q(_0ut_26), .clk(Reloj), .clr(Reset));
  Register #(.width(32)) register_32 (.D(Instruc_2), .en(EN7), .Q(_0ut_30), .clk(Reloj), .clr(Reset));
  Comparator #(.width(16)) comparator_1 (.a(STAG), .b(Addres[19:4]), .eq(comparator_1_eq));  // open: gt, lt
  Register #(.width(32)) register_33 (.D(Instruc_3), .en(EN_0), .Q(_0ut_3), .clk(Reloj), .clr(Reset));
  Register #(.width(32)) register_34 (.D(Instruc_3), .en(EN_1), .Q(_0ut_7), .clk(Reloj), .clr(Reset));
  Register #(.width(32)) register_35 (.D(Instruc_3), .en(EN_2), .Q(_0ut_11), .clk(Reloj), .clr(Reset));
  Register #(.width(32)) register_36 (.D(Instruc_3), .en(EN_3), .Q(_0ut_15), .clk(Reloj), .clr(Reset));
  Register #(.width(32)) register_37 (.D(Instruc_3), .en(EN_4), .Q(_0ut_19), .clk(Reloj), .clr(Reset));
  Register #(.width(32)) register_38 (.D(Instruc_3), .en(EN_5), .Q(_0ut_23), .clk(Reloj), .clr(Reset));
  Register #(.width(32)) register_39 (.D(Instruc_3), .en(EN_6), .Q(_0ut_27), .clk(Reloj), .clr(Reset));
  Register #(.width(32)) register_40 (.D(Instruc_3), .en(EN7), .Q(_0ut_31), .clk(Reloj), .clr(Reset));
  and and_1 (Is_in_Cache, comparator_1_eq, is_valid);
  D_Flip_Flop d_ff_1 (.clk(Reloj), .D(Valido), .Q(v0), .en(EN_0), .reset(Reset));  // open: Qn, preset
  D_Flip_Flop d_ff_2 (.clk(Reloj), .D(Valido), .Q(v1), .en(EN_1), .reset(Reset));  // open: Qn, preset
  D_Flip_Flop d_ff_3 (.clk(Reloj), .D(Valido), .Q(v2), .en(EN_2), .reset(Reset));  // open: Qn, preset
  D_Flip_Flop d_ff_4 (.clk(Reloj), .D(Valido), .Q(v3), .en(EN_3), .reset(Reset));  // open: Qn, preset
  D_Flip_Flop d_ff_5 (.clk(Reloj), .D(Valido), .Q(v4), .en(EN_4), .reset(Reset));  // open: Qn, preset
  D_Flip_Flop d_ff_6 (.clk(Reloj), .D(Valido), .Q(v5), .en(EN_5), .reset(Reset));  // open: Qn, preset
  D_Flip_Flop d_ff_7 (.clk(Reloj), .D(Valido), .Q(v6), .en(EN_6), .reset(Reset));  // open: Qn, preset
  D_Flip_Flop d_ff_8 (.clk(Reloj), .D(Valido), .Q(v7), .en(EN7), .reset(Reset));  // open: Qn, preset
  and and_2 (Invalido, ~R_W_Cach, ~Is_in_Cache);  // AND_Gate

  // Other names for the same wires on the sheet: CLK = Reloj; Inst_0[31:0] = Instruc_0; Inst_1[31:0] = Instruc_1;
  //   Inst_2[31:0] = Instruc_2; Inst_3[31:0] = Instruc_3; Offset[1:0] = Addres[3:2]; PC[31:0] = Addres;
  //   R_W = R_W_Cach; Index[2:0] = Addres[6:4]; tag[15:0] = Addres[19:4]

  // Notes on the sheet:
  //   Entradas
  //   Selector
  //   Descomposicion de Direccion
  //   Tags
  //   Memoria Cache
  //   Data
  //   Buscandolo en la Cache
  //   Valido
  //   Buscar en RAM
endmodule

module Entrada_Adrees (
  input  [31:0] Rs,
  input  [31:0] Valor_Inmediato,
  input  [31:0] SP
);

  wire [15:0] SW;
  wire [31:0] adder_1_out;

  Adder #(.width(32)) adder_1 (
    .a(Rs), .b({{17{Valor_Inmediato[15]}}, Valor_Inmediato[14:0]}),
    .out({adder_1_out[31:20], SW, adder_1_out[3:0]}));  // open: cin, cout

  // Other names for the same wires on the sheet: Inmediato[31:0] = {{17{Valor_Inmediato[15]}}, Valor_Inmediato[14:0]};
  //   SP_t[15:0] = SP[19:4]

  // Notes on the sheet:
  //   Entradas
  //   Entrada Tipo I
  //   Tipo R
endmodule
