// Logisim project Control Unit.circ as structural Verilog: 3 circuits, main circuit Contador de Ciclos
module Contador_de_Ciclos (
  input  [3:0] Read_Time,
  input  [3:0] Write_Time,
  input  Reloj,
  input  R_W,
  input  in_5,
  input  in_6,
  output WAIT
);

  wire [3:0] counter_1_q, RT__WT;

  Multiplexer #(.width(4), .enable("false")) multiplexer_1 (.in0(Read_Time), .in1(Write_Time), .out(RT__WT), .sel(R_W));
  Counter #(.width(4), .max('hf)) counter_1 (.count(in_5), .Q(counter_1_q), .clk(Reloj));  // open: load, D, carry, clr
  Comparator #(.width(4)) comparator_1 (.a(counter_1_q), .b(RT__WT), .eq(WAIT));  // open: gt, lt

  // Other names for the same wires on the sheet: CLK = Reloj; CS = in_5; RST = in_6

  // Notes on the sheet:
  //   Entradas de Tiempo
  //   Contador de Ciclos del Reloj
endmodule

module CONTROL_UNIT (
  input  in_1,
  input  Reloj,
  input  Reset,
  input  [3:0] in_4,
  input  [3:0] Read_Time,
  input  [3:0] Write_Time,
  input  HINT,
  input  DIRTY,
  output SET_SP,
  output out_10,
  output out_11,
  output out_12,
  output VALID,
  output CLEAN,
  output CS,
  output RWRF,
  output out_17,
  output RW_RAM,
  output LSP,
  output RW_CACHE
);

  wire and_1_out, CLEAN1, CLEAN2, CS1, CS2, CS3, CS4, CS5, D1, D2, d_ff_1_q, d_ff_2_q, d_ff_3_q, d_ff_4_q,
       d_ff_6_q, demultiplexer_1_out0, demultiplexer_2_out0, demultiplexer_2_out4, demultiplexer_2_out6,
       demultiplexer_2_out7, demultiplexer_2_out8, demultiplexer_2_out9, EN, LSP1, LSP2, multiplexer_1_out,
       not_1_out, not_3_out, or_1_out, or_11_out, RRW1, RRW2, RRW3, RRW4, RW_CACHE_t, RW_RF1, RW_RF2, RW_RF4,
       RWC1, RWC2, RWC3, RWC4, tiempo_rw_1_finish, tiempo_rw_4_finish, tiempo_rw_5_finish, V1, V2, V3;

  D_Flip_Flop d_ff_1 (.clk(Reloj), .D(or_1_out), .Q(d_ff_1_q), .preset(multiplexer_1_out));  // open: Qn, en, reset
  buf or_1 (or_1_out, demultiplexer_1_out0);  // OR_Gate
  Multiplexer #(.enable("false")) multiplexer_1 (.in0(EN), .in1(1'b0), .out(multiplexer_1_out), .sel(not_1_out));
  not not_1 (not_1_out, Reset);
  not not_2 (EN, in_1);
  Demultiplexer #(.enable("false")) demultiplexer_1 (
    .out0(demultiplexer_1_out0), .out1(SET_SP), .in(d_ff_1_q), .sel(and_1_out));
  and and_1 (and_1_out, EN, not_3_out);
  not not_3 (not_3_out, Reset);
  or or_2 (LSP, LSP1, LSP2);
  or or_3 (RWRF, RW_RF1, RW_RF2, LSP2, RW_RF4);
  or or_4 (out_17, D1, D2);
  TIEMPO_RW tiempo_rw_1 (
    .RST(Reset), .INIT(SET_SP), .HINT(HINT), .DIRTY(DIRTY), .rw(1'b0), .FINISH(tiempo_rw_1_finish),
    .VALIDO(V1), .RW_CACHE(RW_CACHE_t), .CHIFT_SELECT(CS1), .in_1(EN), .in_3(Reloj), .in_8(Read_Time),
    .in_9(Write_Time));  // open: ENSUCIAR, CLEAN, RW_RAM
  or or_5 (VALID, V1, V2, V3);
  or or_6 (CLEAN, CLEAN1, CLEAN2);
  or or_7 (RW_RAM, RRW1, RRW2, RRW3, RRW4);
  D_Flip_Flop #(.trigger("falling")) d_ff_2 (
    .clk(Reloj), .D(tiempo_rw_1_finish), .Q(d_ff_2_q), .reset(Reset));  // open: Qn, preset, en
  or or_8 (CS, CS1, CS2, CS3, CS4, CS5);
  or or_9 (RW_CACHE, RW_CACHE_t, RWC1, RWC2, RWC3, RWC4);
  D_Flip_Flop #(.trigger("falling")) d_ff_3 (
    .clk(Reloj), .D(d_ff_6_q), .Q(d_ff_3_q), .reset(Reset));  // open: Qn, preset, en
  Demultiplexer #(.select(4)) demultiplexer_2 (
    .out0(demultiplexer_2_out0), .out1(RW_RF1), .out2(RW_RF2), .out4(demultiplexer_2_out4), .out5(LSP2),
    .out6(demultiplexer_2_out6), .out7(demultiplexer_2_out7), .out8(demultiplexer_2_out8),
    .out9(demultiplexer_2_out9), .out10(RW_RF4), .in(out_10), .sel(in_4), .en(EN));  // open: out3, out11, out12, out13, out14, out15
  or or_10 (out_10, d_ff_3_q, d_ff_2_q);
  D_Flip_Flop #(.trigger("falling")) d_ff_4 (
    .clk(Reloj), .D(demultiplexer_2_out4), .Q(d_ff_4_q));  // open: Qn, preset, en, reset
  TIEMPO_RW tiempo_rw_2 (
    .RST(Reset), .INIT(demultiplexer_2_out6), .HINT(HINT), .DIRTY(DIRTY), .rw(1'b0), .FINISH(LSP1),
    .VALIDO(V2), .CLEAN(CLEAN1), .RW_CACHE(RWC1), .CHIFT_SELECT(CS2), .RW_RAM(RRW1), .in_1(EN), .in_3(Reloj),
    .in_8(Read_Time), .in_9(Write_Time));  // open: ENSUCIAR
  TIEMPO_RW tiempo_rw_3 (
    .RST(Reset), .INIT(demultiplexer_2_out7), .HINT(HINT), .DIRTY(DIRTY), .rw(1'b1), .FINISH(LSP2),
    .ENSUCIAR(D1), .RW_CACHE(RWC2), .CHIFT_SELECT(CS3), .RW_RAM(RRW2), .in_1(EN), .in_3(Reloj),
    .in_8(Read_Time), .in_9(Write_Time));  // open: VALIDO, CLEAN
  D_Flip_Flop #(.trigger("falling")) d_ff_5 (.clk(Reloj), .D(RW_RF4), .Q(out_12));  // open: Qn, preset, en, reset
  TIEMPO_RW tiempo_rw_4 (
    .RST(Reset), .INIT(demultiplexer_2_out8), .HINT(HINT), .DIRTY(DIRTY), .rw(1'b1),
    .FINISH(tiempo_rw_4_finish), .ENSUCIAR(D2), .RW_CACHE(RWC3), .CHIFT_SELECT(CS4), .RW_RAM(RRW3),
    .in_1(EN), .in_3(Reloj), .in_8(Read_Time), .in_9(Write_Time));  // open: VALIDO, CLEAN
  TIEMPO_RW tiempo_rw_5 (
    .RST(Reset), .INIT(demultiplexer_2_out9), .HINT(HINT), .DIRTY(DIRTY), .rw(1'b0),
    .FINISH(tiempo_rw_5_finish), .VALIDO(V3), .CLEAN(CLEAN2), .RW_CACHE(RWC4), .CHIFT_SELECT(CS5),
    .RW_RAM(RRW4), .in_1(EN), .in_3(Reloj), .in_8(Read_Time), .in_9(Write_Time));  // open: ENSUCIAR
  or or_11 (or_11_out, RW_RF1, RW_RF2, d_ff_4_q, LSP2, LSP1, LSP2, tiempo_rw_4_finish, tiempo_rw_5_finish, out_12);
  or or_12 (out_11, demultiplexer_2_out0, or_11_out);
  D_Flip_Flop #(.trigger("falling")) d_ff_6 (
    .clk(Reloj), .D(out_11), .Q(d_ff_6_q), .reset(Reset));  // open: Qn, preset, en

  // Other names for the same wires on the sheet: CLK = Reloj; KBDENABLE = out_12; LI = out_10; LOAD_PC = out_11;
  //   Op[3:0] = in_4; R[3:0] = Read_Time; RST = Reset; RW_RF3 = LSP2; W[3:0] = Write_Time

  // Notes on the sheet:
  //   INDLE
  //   Control Unit
  //   CACHE LOAD
  //   MEMORIA
  //   POP OPERATION
  //   PUSH OPERATION
  //   STORE
  //   BRANCH OPERATION
  //   MOV OPERATION
  //   ALU- INMEDIATA -LOGICAL OPERATION
  //   TTY
  //   RADOMOPERATION
endmodule

module TIEMPO_RW (
  input  in_1,
  input  RST,
  input  in_3,
  input  INIT,
  input  HINT,
  input  DIRTY,
  input  rw,
  input  [3:0] in_8,
  input  [3:0] in_9,
  output FINISH,
  output VALIDO,
  output ENSUCIAR,
  output CLEAN,
  output RW_CACHE,
  output CHIFT_SELECT,
  output RW_RAM
);

  wire CS1, CS2, CS3, CS4, D1, D3, d_ff_1_q, demultiplexer_1_out0, demultiplexer_1_out1,
       demultiplexer_2_out0, demultiplexer_3_out0, demultiplexer_4_out1, demultiplexer_5_out0,
       demultiplexer_5_out1, demultiplexer_6_out0, demultiplexer_7_out0, demultiplexer_8_out0,
       demultiplexer_8_out1, demultiplexer_9_out0, F1, F3, F5, or_1_out, or_2_out, or_3_out, or_4_out, WAIT;

  D_Flip_Flop #(.trigger("falling")) d_ff_1 (
    .clk(in_3), .D(INIT), .Q(d_ff_1_q), .en(in_1), .reset(RST));  // open: Qn, preset
  Contador_de_Ciclos contador_de_ciclos_1 (
    .Read_Time(in_8), .Write_Time(in_9), .Reloj(in_3), .R_W(rw), .in_5(CHIFT_SELECT), .in_6(RST), .WAIT(WAIT));
  Demultiplexer demultiplexer_1 (
    .out0(demultiplexer_1_out0), .out1(demultiplexer_1_out1), .in(d_ff_1_q), .sel(rw));  // open: en
  Demultiplexer demultiplexer_2 (
    .out0(demultiplexer_2_out0), .out1(D1), .in(demultiplexer_1_out1), .sel(HINT));  // open: en
  Demultiplexer demultiplexer_3 (
    .out0(demultiplexer_3_out0), .out1(F1), .in(demultiplexer_1_out0), .sel(HINT));  // open: en
  Demultiplexer demultiplexer_4 (
    .out0(D3), .out1(demultiplexer_4_out1), .in(demultiplexer_2_out0), .sel(DIRTY));  // open: en
  Demultiplexer demultiplexer_5 (
    .out0(demultiplexer_5_out0), .out1(demultiplexer_5_out1), .in(demultiplexer_3_out0), .sel(DIRTY));  // open: en
  or or_1 (or_1_out, demultiplexer_8_out0, demultiplexer_5_out0);
  or or_2 (or_2_out, demultiplexer_5_out1, demultiplexer_6_out0);
  or or_3 (or_3_out, demultiplexer_7_out0, demultiplexer_4_out1);
  D_Flip_Flop #(.trigger("falling")) d_ff_2 (
    .clk(in_3), .D(or_2_out), .Q(CS2), .en(in_1), .reset(RST));  // open: Qn, preset
  D_Flip_Flop #(.trigger("falling")) d_ff_3 (
    .clk(in_3), .D(or_3_out), .Q(CS4), .en(in_1), .reset(RST));  // open: Qn, preset
  D_Flip_Flop #(.trigger("falling")) d_ff_4 (
    .clk(in_3), .D(or_1_out), .Q(CS1), .en(in_1), .reset(RST));  // open: Qn, preset
  Demultiplexer demultiplexer_6 (.out0(demultiplexer_6_out0), .out1(CLEAN), .in(CS2), .sel(WAIT));  // open: en
  Demultiplexer demultiplexer_7 (.out0(demultiplexer_7_out0), .out1(F5), .in(CS4), .sel(WAIT));  // open: en
  Demultiplexer demultiplexer_8 (
    .out0(demultiplexer_8_out0), .out1(demultiplexer_8_out1), .in(CS1), .sel(WAIT));  // open: en
  or or_4 (or_4_out, demultiplexer_9_out0, CLEAN);
  D_Flip_Flop #(.trigger("falling")) d_ff_5 (
    .clk(in_3), .D(demultiplexer_8_out1), .Q(VALIDO), .en(in_1), .reset(RST));  // open: Qn, preset
  D_Flip_Flop #(.trigger("falling")) d_ff_6 (
    .clk(in_3), .D(or_4_out), .Q(CS3), .en(in_1), .reset(RST));  // open: Qn, preset
  Demultiplexer demultiplexer_9 (.out0(demultiplexer_9_out0), .out1(F3), .in(CS3), .sel(WAIT));  // open: en
  or or_5 (ENSUCIAR, D1, CS4, D3);
  or or_6 (RW_RAM, CS2, CS4);
  or or_7 (FINISH, F1, VALIDO, F3, D1, F5, D3);
  or or_8 (RW_CACHE, D1, CS4, D3, VALIDO, CS3);
  or or_9 (CHIFT_SELECT, CS1, CS2, VALIDO, CS3, CS4);

  // Other names for the same wires on the sheet: CLK = in_3; CS = CHIFT_SELECT; EN = in_1; RRW1 = CS2; F4 = D1;
  //   RW1 = D1; D2 = CS4; RRW2 = CS4; RW2 = CS4; F6 = D3; RW3 = D3; CS5 = VALIDO; F2 = VALIDO; RW4 = VALIDO;
  //   RW5 = CS3

  // Notes on the sheet:
  //   LEER
  //   HINT
  //   MISS
  //   ESCRIBE DIRECTAMENTE
  //   ESCRIBE ||RESCRIBE DEPENDIENDO  DEL DIRTY 
  //   EESCRIBE  LA INFO ANTIGUA EN  LA RAM 
  //   ESCRIBIR
  //   ESCRIBIR
  //   ESCRIBE LA INFO NUEVA EN LA CACHE 
  //   LEER
  //   CACHE OPERATION
  //   RAM OPERATION
endmodule
