// Logisim project INVERTER.circ as structural Verilog
module INVERTER (
  input  [31:0] RAM_OUT1,
  input  [31:0] RAM_OUT2,
  input  [31:0] RAM_OUT3,
  input  [31:0] RAM_OUT4,
  output [31:0] out_5,
  output [31:0] out_6,
  output [31:0] out_7,
  output [31:0] out_8
);


  assign out_5 = {RAM_OUT1[7:0], RAM_OUT1[15:8], RAM_OUT1[23:16], RAM_OUT1[31:24]};
  assign out_6 = {RAM_OUT2[7:0], RAM_OUT2[15:8], RAM_OUT2[23:16], RAM_OUT2[31:24]};
  assign out_7 = {RAM_OUT3[7:0], RAM_OUT3[15:8], RAM_OUT3[23:16], RAM_OUT3[31:24]};
  assign out_8 = {RAM_OUT4[7:0], RAM_OUT4[15:8], RAM_OUT4[23:16], RAM_OUT4[31:24]};

  // Notes on the sheet:
  //   INVERTIR LAS ENTRADAS DE LA RAM EN LITTLE EDIAN
endmodule
