// Logisim project InstructionDecoder.circ as structural Verilog
module InstructionDec (
  input  [31:0] Instruccion,
  input  in_2,
  input  in_3,
  output [5:0] Function,
  output [4:0] Shamt,
  output [4:0] Rd,
  output [4:0] Rt,
  output [4:0] Rs,
  output [15:0] Offset,
  output [25:0] Destino,
  output [5:0] OP_Code
);


  assign Destino = Instruccion[25:0];
  assign Function = Instruccion[5:0];
  assign Offset = Instruccion[15:0];
  assign OP_Code = Instruccion[31:26];
  assign Rd = Instruccion[15:11];
  assign Rs = Instruccion[25:21];
  assign Rt = Instruccion[20:16];
  assign Shamt = Instruccion[10:6];

  // Other names for the same wires on the sheet: CLK = in_3; Instruction[31:0] = Instruccion; RST = in_2

  // Notes on the sheet:
  //   INPUTS
  //   Instrucciones de Tipo R:
  //   OP-Code: (6-bits) , Rs (5-bits)  , Rt (5-bits) , Rd(5-bits)  , Shamt(5-bits) , Function(6-bits)  
  //   Instrucciones de Tipo I
  //   OP-Code: (6-bits) , Rs (5-bits)  , Rt (5-bits) , Imm-Constante-Offset 16-bits
  //   Instrucciones de Tipo J
  //   OP-Code: (6-bits) , addr(destino) 26-bits
  //   Divide la  Instruccion
  //   OUTPUTS
endmodule

module DivideOpCode (
  input  [5:0] OP_Code,
  output Op_00_0000,
  output Op_11_1000,
  output Op_11_1111,
  output I,
  output J,
  output R
);

  wire and_1_out, and_2_out, and_4_out, and_5_out, and_6_out, and_7_out, and_8_out, and_9_out, and_10_out,
       and_11_out, and_12_out, and_13_out, and_14_out, and_15_out, and_17_out, and_18_out, and_19_out,
       and_20_out;

  and and_1 (and_1_out, ~OP_Code[0], OP_Code[1], ~OP_Code[2]);  // AND_Gate
  and and_2 (and_2_out, ~OP_Code[3], ~OP_Code[4], ~OP_Code[5]);  // AND_Gate
  and and_3 (J, and_1_out, and_2_out);
  and and_4 (and_4_out, ~OP_Code[4], ~OP_Code[5]);  // AND_Gate
  and and_5 (and_5_out, ~OP_Code[4], OP_Code[5]);  // AND_Gate
  and and_6 (and_6_out, ~OP_Code[0], ~OP_Code[2], OP_Code[3]);  // AND_Gate
  and and_7 (and_7_out, ~OP_Code[0], ~OP_Code[1], OP_Code[2]);  // AND_Gate
  and and_8 (and_8_out, OP_Code[1], OP_Code[2], ~OP_Code[3]);  // AND_Gate
  and and_9 (and_9_out, OP_Code[0], ~OP_Code[1], ~OP_Code[3]);  // AND_Gate
  and and_10 (and_10_out, OP_Code[0], OP_Code[1], ~OP_Code[2]);  // AND_Gate
  and and_11 (and_11_out, and_6_out, and_4_out);
  and and_12 (and_12_out, and_7_out, and_4_out);
  and and_13 (and_13_out, and_8_out, and_4_out);
  and and_14 (and_14_out, and_9_out, and_4_out);
  and and_15 (and_15_out, and_10_out, and_5_out);
  and and_16 (Op_11_1111, OP_Code[0], OP_Code[1], OP_Code[2], OP_Code[3], OP_Code[4], OP_Code[5]);
  and and_17 (and_17_out, ~OP_Code[0], ~OP_Code[1], ~OP_Code[2]);  // AND_Gate
  and and_18 (and_18_out, OP_Code[3], OP_Code[4], OP_Code[5]);
  and and_19 (and_19_out, ~OP_Code[0], ~OP_Code[1], ~OP_Code[2]);  // AND_Gate
  and and_20 (and_20_out, ~OP_Code[3], ~OP_Code[4], ~OP_Code[5]);  // AND_Gate
  and and_21 (Op_11_1000, and_17_out, and_18_out);
  and and_22 (Op_00_0000, and_19_out, and_20_out);
  or or_1 (I, and_11_out, and_12_out, and_13_out, and_14_out, and_15_out);
  or or_2 (R, Op_11_1111, Op_11_1000, Op_00_0000);

  // Other names for the same wires on the sheet: _00_0000 = Op_00_0000; _11_1000 = Op_11_1000; _11_1111 = Op_11_1111;
  //   B0 = OP_Code[0]; B1 = OP_Code[1]; B2 = OP_Code[2]; B3 = OP_Code[3]; B4 = OP_Code[4]; B5 = OP_Code[5]

  // Notes on the sheet:
  //   OP-Code TIPO J
  //   OP-Code TIPO I
  //   OP-Code TIPO R
endmodule

module ALUOP_DECODER (
  input  [5:0] OP_Code,
  input  [5:0] Function,
  output [3:0] ALUOP,
  output PC__4,
  output Inmediate,
  output HILO
);

  wire _00_0000, _01_1000, _01_1001, _01_1010, _01_1011, _10_0000, _10_0010, _10_0100, _10_0101, _10_0111,
       _10_1000, _10_1010, _10_1011, ADD, ADDI, AND, and_1_out, and_2_out, and_3_out, and_4_out, and_5_out,
       and_7_out, and_8_out, and_10_out, and_11_out, and_13_out, and_16_out, and_17_out, and_18_out,
       and_19_out, and_20_out, and_21_out, and_22_out, and_23_out, and_24_out, and_26_out, and_31_out,
       and_32_out, and_33_out, and_34_out, and_35_out, and_36_out, and_37_out, and_38_out, and_39_out,
       and_40_out, and_46_out, and_47_out, and_48_out, and_49_out, and_50_out, and_51_out, and_52_out,
       and_53_out, ANDI, DIV, DIVU, MULT, MULU, NADA, NOR, OR, or_1_out, or_2_out, or_3_out, or_4_out,
       or_5_out, or_6_out, or_8_out, or_9_out, or_10_out, or_11_out, or_12_out, or_13_out, ORI, SLT, SLTI,
       SLTIU, SLTU, SUBS, XOR, XORI;

  and and_1 (and_1_out, ~OP_Code[0], ~OP_Code[1], ~OP_Code[2]);  // AND_Gate
  and and_2 (and_2_out, ~OP_Code[3], ~OP_Code[4], ~OP_Code[5]);  // AND_Gate
  and and_3 (and_3_out, ~OP_Code[0], ~OP_Code[1], ~OP_Code[2]);  // AND_Gate
  and and_4 (and_4_out, OP_Code[3], ~OP_Code[4], ~OP_Code[5]);  // AND_Gate
  and and_5 (and_5_out, ~Function[0], ~Function[1], ~Function[2]);  // AND_Gate
  and and_6 (_10_0000, and_5_out, and_7_out);
  and and_7 (and_7_out, ~Function[3], ~Function[4], Function[5]);  // AND_Gate
  and and_8 (and_8_out, ~Function[0], Function[1], ~Function[2]);  // AND_Gate
  and and_9 (_10_0010, and_8_out, and_10_out);
  and and_10 (and_10_out, ~Function[3], ~Function[4], Function[5]);  // AND_Gate
  and and_11 (and_11_out, Function[0], Function[1], Function[2]);
  and and_12 (_10_0111, and_11_out, and_13_out);
  and and_13 (and_13_out, ~Function[3], ~Function[4], Function[5]);  // AND_Gate
  and and_14 (_00_0000, and_1_out, and_2_out);
  and and_15 (ADDI, and_3_out, and_4_out);
  and and_16 (and_16_out, OP_Code[3], ~OP_Code[4], ~OP_Code[5]);  // AND_Gate
  and and_17 (and_17_out, OP_Code[3], ~OP_Code[4], ~OP_Code[5]);  // AND_Gate
  and and_18 (and_18_out, ~Function[0], ~Function[1], ~Function[2]);  // AND_Gate
  and and_19 (and_19_out, Function[3], Function[4], ~Function[5]);  // AND_Gate
  and and_20 (and_20_out, Function[0], ~Function[1], ~Function[2]);  // AND_Gate
  and and_21 (and_21_out, Function[3], Function[4], ~Function[5]);  // AND_Gate
  and and_22 (and_22_out, ~Function[0], ~Function[1], ~Function[2]);  // AND_Gate
  and and_23 (and_23_out, Function[3], ~Function[4], Function[5]);  // AND_Gate
  and and_24 (and_24_out, ~OP_Code[0], ~OP_Code[1], OP_Code[2]);  // AND_Gate
  and and_25 (ANDI, and_24_out, and_16_out);
  and and_26 (and_26_out, OP_Code[0], ~OP_Code[1], OP_Code[2]);  // AND_Gate
  and and_27 (ORI, and_26_out, and_17_out);
  and and_28 (_01_1000, and_18_out, and_19_out);
  and and_29 (_01_1001, and_20_out, and_21_out);
  and and_30 (_10_1000, and_22_out, and_23_out);
  or or_1 (or_1_out, ADD, ADDI);
  or or_2 (or_2_out, AND, ANDI);
  or or_3 (or_3_out, OR, ORI);
  or or_4 (or_4_out, XOR, XORI);
  or or_5 (or_5_out, SLTU, SLTIU);
  or or_6 (or_6_out, SLT, SLTI);
  and and_31 (and_31_out, ~OP_Code[0], OP_Code[1], OP_Code[2]);  // AND_Gate
  and and_32 (and_32_out, OP_Code[3], ~OP_Code[4], ~OP_Code[5]);  // AND_Gate
  and and_33 (and_33_out, ~OP_Code[0], OP_Code[1], ~OP_Code[2]);  // AND_Gate
  and and_34 (and_34_out, OP_Code[3], ~OP_Code[4], ~OP_Code[5]);  // AND_Gate
  and and_35 (and_35_out, ~Function[0], Function[1], ~Function[2]);  // AND_Gate
  and and_36 (and_36_out, Function[3], Function[4], ~Function[5]);  // AND_Gate
  and and_37 (and_37_out, Function[0], Function[1], ~Function[2]);  // AND_Gate
  and and_38 (and_38_out, Function[3], Function[4], ~Function[5]);  // AND_Gate
  and and_39 (and_39_out, ~Function[0], Function[1], ~Function[2]);  // AND_Gate
  and and_40 (and_40_out, Function[3], ~Function[4], Function[5]);  // AND_Gate
  and and_41 (XORI, and_31_out, and_32_out);
  and and_42 (SLTI, and_33_out, and_34_out);
  and and_43 (_01_1010, and_35_out, and_36_out);
  and and_44 (_01_1011, and_37_out, and_38_out);
  and and_45 (_10_1010, and_39_out, and_40_out);
  Priority_Encoder #(.select(4)) priority_encoder_1 (
    .in0(or_1_out), .in1(SUBS), .in2(or_2_out), .in3(or_3_out), .in4(NOR), .in5(or_4_out), .in6(or_5_out),
    .in7(or_6_out), .in8(MULU), .in9(MULT), .in10(DIVU), .in11(DIV), .in15(NADA), .out(ALUOP));  // open: in12, in13, in14, gs, en_out, en_in
  and and_46 (and_46_out, ~Function[0], ~Function[1], Function[2]);  // AND_Gate
  and and_47 (and_47_out, ~Function[3], ~Function[4], Function[5]);  // AND_Gate
  and and_48 (and_48_out, Function[0], ~Function[1], Function[2]);  // AND_Gate
  and and_49 (and_49_out, ~Function[3], ~Function[4], Function[5]);  // AND_Gate
  and and_50 (and_50_out, Function[0], Function[1], ~Function[2]);  // AND_Gate
  and and_51 (and_51_out, Function[3], ~Function[4], Function[5]);  // AND_Gate
  nand nand_1 (PC__4, ALUOP[0], ALUOP[1], ALUOP[2], ALUOP[3]);
  and and_52 (and_52_out, OP_Code[0], OP_Code[1], ~OP_Code[2]);  // AND_Gate
  and and_53 (and_53_out, OP_Code[3], ~OP_Code[4], ~OP_Code[5]);  // AND_Gate
  and and_54 (_10_0100, and_46_out, and_47_out);
  and and_55 (_10_0101, and_48_out, and_49_out);
  and and_56 (_10_1011, and_50_out, and_51_out);
  or or_7 (HILO, MULU, MULT, DIVU, DIV);
  and and_57 (SLTIU, and_52_out, and_53_out);
  or or_8 (or_8_out, ADD, ADDI);
  or or_9 (or_9_out, AND, ANDI);
  or or_10 (or_10_out, OR, ORI);
  or or_11 (or_11_out, XOR, XORI);
  or or_12 (or_12_out, SLTU, SLTIU);
  or or_13 (or_13_out, SLT, SLTI);
  and and_58 (ADD, _00_0000, _10_0000);
  and and_59 (SUBS, _00_0000, _10_0010);
  and and_60 (MULT, _00_0000, _01_1000);
  and and_61 (MULU, _00_0000, _01_1001);
  and and_62 (DIV, _00_0000, _01_1010);
  and and_63 (DIVU, _00_0000, _01_1011);
  and and_64 (AND, _00_0000, _10_0100);
  and and_65 (OR, _00_0000, _10_0101);
  and and_66 (NOR, _00_0000, _10_0111);
  and and_67 (XOR, _00_0000, _10_1000);
  and and_68 (SLT, _00_0000, _10_1010);
  and and_69 (SLTU, _00_0000, _10_1011);
  and and_70 (NADA, ~or_8_out, ~SUBS, ~or_9_out, ~or_10_out, ~NOR, ~or_11_out, ~or_12_out, ~or_13_out, ~MULU, ~MULT, ~DIVU, ~DIV);  // AND_Gate
  or or_14 (Inmediate, ADDI, ANDI, ORI, XORI, SLTIU, SLTI);

  // Other names for the same wires on the sheet: F0 = Function[0]; F1 = Function[1]; F2 = Function[2];
  //   F3 = Function[3]; F4 = Function[4]; F5 = Function[5]; B0 = OP_Code[0]; B1 = OP_Code[1]; B2 = OP_Code[2];
  //   B3 = OP_Code[3]; B4 = OP_Code[4]; B5 = OP_Code[5]

  // Notes on the sheet:
  //   INPUTS
  //   OPCODE R
  //   DECODIFICA LA OPERACION LOGICA - ARITEMTICA PARA QUE SEA ENTENDIDA POR EL ALU
  //   FUNCTION 
  //   OUTPUT
  //   OPCODE I
  //   OPCODE R + FUNCTION
endmodule

module MOV_Op (
  input  [5:0] OP_Code,
  input  [5:0] Function,
  output RW,
  output [1:0] Selector_Input_RF,
  output SHI,
  output SLo
);

  wire _00_0000, _01_0000, _01_0010, and_1_out, and_2_out, and_6_out, and_7_out, and_9_out, and_10_out,
       and_11_out;

  and and_1 (and_1_out, ~OP_Code[0], ~OP_Code[1], ~OP_Code[2]);  // AND_Gate
  and and_2 (and_2_out, ~OP_Code[3], ~OP_Code[4], ~OP_Code[5]);  // AND_Gate
  and and_3 (_00_0000, and_1_out, and_2_out);
  and and_4 (SHI, _00_0000, _01_0000);
  and and_5 (SLo, _00_0000, _01_0010);
  and and_6 (and_6_out, ~Function[0], ~Function[1], ~Function[2]);  // AND_Gate
  and and_7 (and_7_out, ~Function[3], Function[4], ~Function[5]);  // AND_Gate
  and and_8 (_01_0000, and_6_out, and_7_out);
  and and_9 (and_9_out, ~SHI, ~SLo);  // AND_Gate
  and and_10 (and_10_out, ~Function[0], Function[1], ~Function[2]);  // AND_Gate
  and and_11 (and_11_out, ~Function[3], Function[4], ~Function[5]);  // AND_Gate
  or or_1 (RW, SHI, SLo);
  and and_12 (_01_0010, and_10_out, and_11_out);
  Priority_Encoder #(.select(2)) priority_encoder_1 (
    .in0(and_9_out), .in1(SHI), .in2(SLo), .out(Selector_Input_RF));  // open: in3, gs, en_out, en_in

  // Other names for the same wires on the sheet: F0 = Function[0]; F1 = Function[1]; F2 = Function[2];
  //   F3 = Function[3]; F4 = Function[4]; F5 = Function[5]; B0 = OP_Code[0]; B1 = OP_Code[1]; B2 = OP_Code[2];
  //   B3 = OP_Code[3]; B4 = OP_Code[4]; B5 = OP_Code[5]; Rd____Hi = SHI; Rd____Lo = SLo

  // Notes on the sheet:
  //   INPUTS
  //   SELECTORES DEL RF
endmodule

module BranchDecoder (
  input  [5:0] OP_Code,
  input  [5:0] Function,
  input  in_3,
  input  in_4,
  input  in_5,
  output [1:0] out_6,
  output BRANCHOP
);

  wire _00BEQ, _00BGTZ, _00BLEZ, _00BLTZ, _00BNE, _01BEQ, _01BGTZ, _01BLEZ, _01BLTZ, _01BNE, and_1_out,
       and_2_out, and_3_out, and_4_out, BEQ, BGTZ, BLEZ, BLTZ, BNE, JUMP, JUMP_REGISTER, NO_OPeration,
       not_1_out, not_2_out, or_1_out, or_2_out, or_3_out, or_4_out, or_5_out;

  and and_1 (and_1_out, ~OP_Code[0], ~OP_Code[1], ~OP_Code[2], ~OP_Code[3], ~OP_Code[4], ~OP_Code[5]);  // AND_Gate
  and and_2 (and_2_out, ~Function[0], ~Function[1], ~Function[2], ~Function[3], ~Function[4], ~Function[5]);  // AND_Gate
  and and_3 (and_3_out, ~OP_Code[0], ~OP_Code[1], ~OP_Code[2], ~OP_Code[3], ~OP_Code[4], ~OP_Code[5]);  // AND_Gate
  and and_4 (and_4_out, ~Function[0], ~Function[1], ~Function[2], Function[3], ~Function[4], ~Function[5]);  // AND_Gate
  and and_5 (NO_OPeration, and_1_out, and_2_out);
  and and_6 (JUMP_REGISTER, and_3_out, and_4_out);
  Demultiplexer #(.enable("false")) demultiplexer_1 (.out0(_00BEQ), .out1(_01BEQ), .in(BEQ), .sel(in_3));
  Demultiplexer #(.enable("false")) demultiplexer_2 (.out0(_00BNE), .out1(_01BNE), .in(BNE), .sel(not_1_out));
  not not_1 (not_1_out, in_3);
  and and_7 (BEQ, ~OP_Code[0], ~OP_Code[1], OP_Code[2], ~OP_Code[3], ~OP_Code[4], ~OP_Code[5]);  // AND_Gate
  and and_8 (BGTZ, OP_Code[0], OP_Code[1], OP_Code[2], ~OP_Code[3], ~OP_Code[4], ~OP_Code[5]);  // AND_Gate
  or or_1 (or_1_out, NO_OPeration, _00BEQ, _00BNE, _00BLEZ, _00BGTZ, _00BLTZ);
  or or_2 (or_2_out, _01BEQ, _01BNE, _01BLEZ, _01BGTZ, _01BLTZ);
  Demultiplexer #(.enable("false")) demultiplexer_3 (.out0(_00BLEZ), .out1(_01BLEZ), .in(BLEZ), .sel(in_4));
  Demultiplexer #(.enable("false")) demultiplexer_4 (.out0(_00BGTZ), .out1(_01BGTZ), .in(BGTZ), .sel(not_2_out));
  not not_2 (not_2_out, in_4);
  or or_3 (or_3_out, or_1_out, 1'b1);
  and and_9 (BNE, OP_Code[0], ~OP_Code[1], OP_Code[2], ~OP_Code[3], ~OP_Code[4], ~OP_Code[5]);  // AND_Gate
  and and_10 (BLTZ, OP_Code[0], ~OP_Code[1], ~OP_Code[2], ~OP_Code[3], ~OP_Code[4], ~OP_Code[5]);  // AND_Gate
  Priority_Encoder #(.select(2)) priority_encoder_1 (
    .in0(or_3_out), .in1(or_2_out), .in2(JUMP), .in3(JUMP_REGISTER), .out(out_6));  // open: gs, en_out, en_in
  Demultiplexer #(.enable("false")) demultiplexer_5 (.out0(_00BLTZ), .out1(_01BLTZ), .in(BLTZ), .sel(in_5));
  and and_11 (BLEZ, ~OP_Code[0], OP_Code[1], OP_Code[2], ~OP_Code[3], ~OP_Code[4], ~OP_Code[5]);  // AND_Gate
  and and_12 (JUMP, ~OP_Code[0], OP_Code[1], ~OP_Code[2], ~OP_Code[3], ~OP_Code[4], ~OP_Code[5]);  // AND_Gate
  or or_4 (or_4_out, NO_OPeration, _00BEQ, _00BNE, _00BLEZ, _00BGTZ, _00BLTZ);
  or or_5 (or_5_out, _01BEQ, _01BNE, _01BLEZ, _01BGTZ, _01BLTZ);
  or or_6 (BRANCHOP, or_4_out, or_5_out, JUMP, JUMP_REGISTER);

  // Other names for the same wires on the sheet: F0 = Function[0]; F1 = Function[1]; F2 = Function[2];
  //   F3 = Function[3]; F4 = Function[4]; F5 = Function[5]; B0 = OP_Code[0]; B1 = OP_Code[1]; B2 = OP_Code[2];
  //   B3 = OP_Code[3]; B4 = OP_Code[4]; B5 = OP_Code[5]; RS_0 = in_5; RS__0 = in_4; RS__RT = in_3

  // Notes on the sheet:
  //   INPUTS
  //   OUTPUTS
endmodule

module MemoryOPDecoder (
  input  [5:0] OP_Code,
  input  [5:0] Function,
  output LoadWord,
  output StoreWord,
  output POP,
  output PUSH
);

  wire and_3_out, and_4_out, and_6_out, and_7_out;

  and and_1 (LoadWord, OP_Code[0], OP_Code[1], ~OP_Code[2], ~OP_Code[3], ~OP_Code[4], OP_Code[5]);  // AND_Gate
  and and_2 (StoreWord, OP_Code[0], OP_Code[1], ~OP_Code[2], OP_Code[3], ~OP_Code[4], OP_Code[5]);  // AND_Gate
  and and_3 (and_3_out, ~OP_Code[0], ~OP_Code[1], ~OP_Code[2], OP_Code[3], OP_Code[4], OP_Code[5]);  // AND_Gate
  and and_4 (and_4_out, ~Function[0], ~Function[1], ~Function[2], ~Function[3], ~Function[4], ~Function[5]);  // AND_Gate
  and and_5 (POP, and_3_out, and_4_out);
  and and_6 (and_6_out, ~OP_Code[0], ~OP_Code[1], ~OP_Code[2], OP_Code[3], OP_Code[4], OP_Code[5]);  // AND_Gate
  and and_7 (and_7_out, Function[0], ~Function[1], ~Function[2], ~Function[3], ~Function[4], ~Function[5]);  // AND_Gate
  and and_8 (PUSH, and_6_out, and_7_out);

  // Other names for the same wires on the sheet: F0 = Function[0]; F1 = Function[1]; F2 = Function[2];
  //   F3 = Function[3]; F4 = Function[4]; F5 = Function[5]; LW = LoadWord; B0 = OP_Code[0]; B1 = OP_Code[1];
  //   B2 = OP_Code[2]; B3 = OP_Code[3]; B4 = OP_Code[4]; B5 = OP_Code[5]; SW = StoreWord

  // Notes on the sheet:
  //   INPUTS
endmodule

module Especiales (
  input  [5:0] OP_Code,
  input  [5:0] Function,
  output HALT,
  output TTYENABLE,
  output Random,
  output KBD
);

  wire and_1_out, and_2_out, and_4_out, and_5_out, and_7_out, and_8_out, and_10_out, and_11_out;

  and and_1 (and_1_out, OP_Code[0], OP_Code[1], OP_Code[2], OP_Code[3], OP_Code[4], OP_Code[5]);
  and and_2 (and_2_out, Function[0], Function[1], Function[2], Function[3], Function[4], Function[5]);
  and and_3 (HALT, and_1_out, and_2_out);
  and and_4 (and_4_out, OP_Code[0], OP_Code[1], OP_Code[2], OP_Code[3], OP_Code[4], OP_Code[5]);
  and and_5 (and_5_out, Function[0], ~Function[1], ~Function[2], ~Function[3], ~Function[4], ~Function[5]);  // AND_Gate
  and and_6 (TTYENABLE, and_4_out, and_5_out);
  and and_7 (and_7_out, OP_Code[0], OP_Code[1], OP_Code[2], OP_Code[3], OP_Code[4], OP_Code[5]);
  and and_8 (and_8_out, ~Function[0], Function[1], ~Function[2], ~Function[3], ~Function[4], ~Function[5]);  // AND_Gate
  and and_9 (Random, and_7_out, and_8_out);
  and and_10 (and_10_out, OP_Code[0], OP_Code[1], OP_Code[2], OP_Code[3], OP_Code[4], OP_Code[5]);
  and and_11 (and_11_out, ~Function[0], ~Function[1], Function[2], ~Function[3], ~Function[4], ~Function[5]);  // AND_Gate
  and and_12 (KBD, and_10_out, and_11_out);

  // Other names for the same wires on the sheet: F0 = Function[0]; F1 = Function[1]; F2 = Function[2];
  //   F3 = Function[3]; F4 = Function[4]; F5 = Function[5]; B0 = OP_Code[0]; B1 = OP_Code[1]; B2 = OP_Code[2];
  //   B3 = OP_Code[3]; B4 = OP_Code[4]; B5 = OP_Code[5]; RND = Random; TTY_ENABLE = TTYENABLE

  // Notes on the sheet:
  //   INPUTS
  //   INPUTS
  //   OUTPUTS
endmodule

module Operation_Decoder (
  input  [5:0] in_1,
  input  [5:0] in_2,
  input  [31:0] INFO__RS,
  input  [31:0] INFO__RT,
  output SelectorSP,
  output [3:0] CU_OP,
  output [1:0] Selector_BC,
  output HILO,
  output [3:0] ALU_OP,
  output SelectorDA,
  output [2:0] SelectorDataIN,
  output [1:0] SelectorB,
  output HALT,
  output [1:0] SELECTADRESS
);

  wire ALU, ALU_4, Branch_OP, comparator_2_eq, HI, Inmediata, KBD, LO, LW, MOV_OP, or_1_out, or_2_out,
       or_5_out, or_6_out, or_7_out, PC_4, POP, PUSH, RND, SW, TTY, tunnel, tunnel_t, tunnel_t_t;
  wire [1:0] branchdecoder_1_out_6, InputRF_Selector;

  Comparator #(.width(32)) comparator_1 (.a(INFO__RS), .b(INFO__RT), .eq(tunnel_t_t));  // open: gt, lt
  or or_1 (or_1_out, LW, SW);
  MemoryOPDecoder memoryopdecoder_1 (
    .OP_Code(in_1), .Function(in_2), .LoadWord(LW), .StoreWord(SW), .POP(POP), .PUSH(PUSH));
  or or_2 (or_2_out, POP, PUSH);
  Comparator #(.width(32)) comparator_2 (.a(INFO__RS), .b({32{1'b0}}), .eq(comparator_2_eq), .lt(tunnel));  // open: gt
  BranchDecoder branchdecoder_1 (
    .OP_Code(in_1), .Function(in_2), .in_3(tunnel_t_t), .in_4(tunnel_t), .in_5(tunnel),
    .out_6(branchdecoder_1_out_6), .BRANCHOP(Branch_OP));
  ALUOP_DECODER aluop_decoder_1 (
    .OP_Code(in_1), .Function(in_2), .ALUOP(ALU_OP), .PC__4(ALU_4), .Inmediate(Inmediata), .HILO(HILO));
  Especiales especiales_1 (.OP_Code(in_1), .Function(in_2), .HALT(HALT), .TTYENABLE(TTY), .Random(RND), .KBD(KBD));
  or or_3 (tunnel_t, comparator_2_eq, tunnel);
  Priority_Encoder #(.select(2)) priority_encoder_1 (
    .in0(1'b1), .in1(or_2_out), .in2(or_1_out), .out(SELECTADRESS));  // open: in3, gs, en_out, en_in
  // Probe on Selector_BC
  Multiplexer #(.width(2), .enable("false")) multiplexer_1 (
    .in0(branchdecoder_1_out_6), .in1(2'b00), .out(Selector_BC), .sel(PC_4));
  MOV_Op mov_op_1 (
    .OP_Code(in_1), .Function(in_2), .RW(MOV_OP), .Selector_Input_RF(InputRF_Selector), .SHI(HI), .SLo(LO));
  or or_4 (PC_4, LW, SW, POP, PUSH, MOV_OP, ALU_4);
  or or_5 (or_5_out, 1'b1, POP);
  or or_6 (or_6_out, LW, Inmediata);
  Priority_Encoder #(.select(1)) priority_encoder_2 (
    .in0(or_5_out), .in1(PUSH), .out(SelectorSP));  // open: gs, en_out, en_in
  Priority_Encoder priority_encoder_3 (
    .in0(1'b1), .in1(HI), .in2(LO), .in3(LW), .in4(POP), .in5(RND), .in6(KBD), .out(SelectorDataIN));  // open: in7, en_in, gs, en_out
  Priority_Encoder #(.select(2)) priority_encoder_4 (
    .in0(1'b1), .in1(Inmediata), .out(SelectorB));  // open: in2, in3, gs, en_out, en_in
  Priority_Encoder #(.select(1)) priority_encoder_5 (
    .in0(1'b1), .in1(or_6_out), .out(SelectorDA));  // open: gs, en_out, en_in
  nand nand_1 (ALU, ALU_OP[0], ALU_OP[1], ALU_OP[2], ALU_OP[3]);
  or or_7 (or_7_out, 1'b1, Branch_OP);
  Priority_Encoder #(.select(4)) priority_encoder_6 (
    .in0(or_7_out), .in1(ALU), .in2(MOV_OP), .in3(HALT), .in4(TTY), .in5(RND), .in6(POP), .in7(PUSH),
    .in8(LW), .in9(SW), .in10(KBD), .out(CU_OP));  // open: in11, in12, in13, in14, in15, gs, en_out, en_in

  // Other names for the same wires on the sheet: Function[5:0] = in_2; INFO_RS[31:0] = INFO__RS;
  //   INFO_RT[31:0] = INFO__RT; OPCOde[5:0] = in_1

  // Notes on the sheet:
  //   INPUTS
  //   ACCEDer a la info de esos registros 
  //   OPERATION DECODER
  //   SELECTOR STACK POINTER
  //   SELECTOR BRANCH CONTROL
  //   OPERACION DEL ALU
  //   SELECTOR DATA ADRESS
  //   SELECTOR DATA IN
  //   SELECTOR B DEL ALU
  //   CONTROL UNIT OPERATION
endmodule
