// Logisim project Register File.circ as structural Verilog: 2 circuits, main circuit Register File
module Register_File (
  input  Reloj,
  input  Reset,
  input  RW,
  input  [31:0] DI,
  input  [4:0] DA,
  input  [4:0] SA,
  input  [4:0] SB,
  input  Mult_or_Div,
  input  [31:0] HI,
  input  [31:0] Lo,
  input  OP_SP,
  input  Set,
  input  Load,
  output [31:0] Output_Hi,
  output [31:0] Output_Lo,
  output [31:0] Output_A,
  output [31:0] Output__B
);

  wire D1, D2, D3, D4, D5, D6, D7, D8, D9, D10, D11, D12, D13, D14, D15, D16, D17, D18, D19, D20, D21, D22,
       D23, D24, D25, D26, D27, D28, D29, D30;
  wire [31:0] multiplexer_3_out, Out1, Out2, Out3, Out4, Out5, Out6, Out7, Out8, Out9, Out10, Out11, Out12,
       Out13, Out14, Out15, Out16, Out17, Out18, Out19, Out20, Out21, Out22, Out23, Out24, Out25, Out26,
       Out27, Out28, Out29, Out30, SP, SP_4, SP_4_t;

  // Probe on DI
  Register #(.width(32)) R1 (.D(DI), .en(D1), .Q(Out1), .clk(Reloj), .clr(Reset));
  Register #(.width(32)) R2 (.D(DI), .en(D2), .Q(Out2), .clk(Reloj), .clr(Reset));
  Register #(.width(32)) R3 (.D(DI), .en(D3), .Q(Out3), .clk(Reloj), .clr(Reset));
  Register #(.width(32)) R4 (.D(DI), .en(D4), .Q(Out4), .clk(Reloj), .clr(Reset));
  Decoder #(.select(5), .disabled(0)) decoder_1 (
    .out1(D1), .out2(D2), .out3(D3), .out4(D4), .out5(D5), .out6(D6), .out7(D7), .out8(D8), .out9(D9),
    .out10(D10), .out11(D11), .out12(D12), .out13(D13), .out14(D14), .out15(D15), .out16(D16), .out17(D17),
    .out18(D18), .out19(D19), .out20(D20), .out21(D21), .out22(D22), .out23(D23), .out24(D24), .out25(D25),
    .out26(D26), .out27(D27), .out28(D28), .out29(D29), .out30(D30), .out31(D30), .sel(DA), .en(RW));  // open: out0
  Register #(.width(32)) R5 (.D(DI), .en(D5), .Q(Out5), .clk(Reloj), .clr(Reset));
  Register #(.width(32)) R6 (.D(DI), .en(D6), .Q(Out6), .clk(Reloj), .clr(Reset));
  Register #(.width(32)) R7 (.D(DI), .en(D7), .Q(Out7), .clk(Reloj), .clr(Reset));
  Register #(.width(32)) R8 (.D(DI), .en(D8), .Q(Out8), .clk(Reloj), .clr(Reset));
  Register #(.width(32)) R9 (.D(DI), .en(D9), .Q(Out9), .clk(Reloj), .clr(Reset));
  Register #(.width(32)) R10 (.D(DI), .en(D10), .Q(Out10), .clk(Reloj), .clr(Reset));
  Register #(.width(32)) R11 (.D(DI), .en(D11), .Q(Out11), .clk(Reloj), .clr(Reset));
  Register #(.width(32)) R12 (.D(DI), .en(D12), .Q(Out12), .clk(Reloj), .clr(Reset));
  Register #(.width(32)) R13 (.D(DI), .en(D13), .Q(Out13), .clk(Reloj), .clr(Reset));
  Register #(.width(32)) R14 (.D(DI), .en(D14), .Q(Out14), .clk(Reloj), .clr(Reset));
  Register #(.width(32)) R15 (.D(DI), .en(D15), .Q(Out15), .clk(Reloj), .clr(Reset));
  Register #(.width(32)) R16 (.D(DI), .en(D16), .Q(Out16), .clk(Reloj), .clr(Reset));
  Multiplexer #(.select(5), .width(32), .enable("false")) multiplexer_1 (
    .in0({32{1'b0}}), .in1(Out1), .in2(Out2), .in3(Out3), .in4(Out4), .in5(Out5), .in6(Out6), .in7(Out7),
    .in8(Out8), .in9(Out9), .in10(Out10), .in11(Out11), .in12(Out12), .in13(Out13), .in14(Out14),
    .in15(Out15), .in16(Out16), .in17(Out17), .in18(Out18), .in19(Out19), .in20(Out20), .in21(Out21),
    .in22(Out22), .in23(Out23), .in24(Out24), .in25(Out25), .in26(Out26), .in27(Out27), .in28(Out28),
    .in29(Out29), .in30(Out30), .in31(SP), .out(Output_A), .sel(SA));
  Register #(.width(32)) R17 (.D(DI), .en(D17), .Q(Out17), .clk(Reloj), .clr(Reset));
  Register #(.width(32)) R18 (.D(DI), .en(D18), .Q(Out18), .clk(Reloj), .clr(Reset));
  Register #(.width(32)) R19 (.D(DI), .en(D19), .Q(Out19), .clk(Reloj), .clr(Reset));
  Register #(.width(32)) R20 (.D(DI), .en(D20), .Q(Out20), .clk(Reloj), .clr(Reset));
  Register #(.width(32)) R21 (.D(DI), .en(D21), .Q(Out21), .clk(Reloj), .clr(Reset));
  Register #(.width(32)) R22 (.D(DI), .en(D22), .Q(Out22), .clk(Reloj), .clr(Reset));
  Register #(.width(32)) R23 (.D(DI), .en(D23), .Q(Out23), .clk(Reloj), .clr(Reset));
  Register #(.width(32)) R24 (.D(DI), .en(D24), .Q(Out24), .clk(Reloj), .clr(Reset));
  Multiplexer #(.select(5), .width(32), .enable("false")) multiplexer_2 (
    .in0({32{1'b0}}), .in1(Out1), .in2(Out2), .in3(Out3), .in4(Out4), .in5(Out5), .in6(Out6), .in7(Out7),
    .in8(Out8), .in9(Out9), .in10(Out10), .in11(Out11), .in12(Out12), .in13(Out13), .in14(Out14),
    .in15(Out15), .in16(Out16), .in17(Out17), .in18(Out18), .in19(Out19), .in20(Out20), .in21(Out21),
    .in22(Out22), .in23(Out23), .in24(Out24), .in25(Out25), .in26(Out26), .in27(Out27), .in28(Out28),
    .in29(Out29), .in30(Out30), .in31(SP), .out(Output__B), .sel(SB));
  Register #(.width(32)) R25 (.D(DI), .en(D25), .Q(Out25), .clk(Reloj), .clr(Reset));
  Register #(.width(32)) R26 (.D(DI), .en(D26), .Q(Out26), .clk(Reloj), .clr(Reset));
  Register #(.width(32)) R27 (.D(DI), .en(D27), .Q(Out27), .clk(Reloj), .clr(Reset));
  Register #(.width(32)) R28 (.D(DI), .en(D28), .Q(Out28), .clk(Reloj), .clr(Reset));
  Register #(.width(32)) R29 (.D(DI), .en(D29), .Q(Out29), .clk(Reloj), .clr(Reset));
  Register #(.width(32)) R30 (.D(DI), .en(D30), .Q(Out30), .clk(Reloj), .clr(Reset));
  Adder #(.width(32)) adder_1 (.a(SP), .b(32'h4), .out(SP_4));  // open: cin, cout
  Subtractor #(.width(32)) subtractor_1 (.a(SP), .b(32'h4), .out(SP_4_t));  // open: bin, bout
  Multiplexer #(.width(32), .enable("false")) multiplexer_3 (
    .in0(SP_4), .in1(SP_4_t), .out(multiplexer_3_out), .sel(OP_SP));
  Stack_Pointer stack_pointer_1 (
    .Reloj(Reloj), .Reset(Reset), .Set(Set), .Load(Load), .Input(multiplexer_3_out), .SP(SP));
  Register #(.width(32)) u_Hi (.D(HI), .en(Mult_or_Div), .Q(Output_Hi), .clk(Reloj), .clr(Reset));
  Register #(.width(32)) u_Lo (.D(Lo), .en(Mult_or_Div), .Q(Output_Lo), .clk(Reloj), .clr(Reset));
  // Probe on Output_A
  // Probe on Output__B

  // Other names for the same wires on the sheet: CLK = Reloj; Input[31:0] = DI; Registro_A[31:0] = Output_A;
  //   Registro_B[31:0] = Output__B; Write_Hi_Lo = Mult_or_Div

  // Notes on the sheet:
  //   Reset
  //   RW
  //   Dato de Entrada
  //   SELECTORES
  //   Data Address
  //   SA
  //   SB
  //   INPUTS
  //   Entradas del Stack Pointer
  //   Ro
  //   Read Or Write
  //   SELECTORES
  //   Selector de Registro A
  //   REGISTROS
  //   Selector de Registro B
  //   Stack Pointer
  //   R31
  //   Nota las operaciones del SP tenemos que ponerlas en un circuito aparte
  //   OUTPUTS
endmodule

module Stack_Pointer (
  input  Reloj,
  input  Reset,
  input  Set,
  input  Load,
  input  [31:0] Input,
  output [31:0] SP
);

  D_Flip_Flop #(.trigger("falling")) d_ff_1 (
    .clk(Reloj), .D(Input[0]), .Q(SP[0]), .preset(Set), .en(Load), .reset(Reset));  // open: Qn
  D_Flip_Flop #(.trigger("falling")) d_ff_2 (
    .clk(Reloj), .D(Input[1]), .Q(SP[1]), .preset(Set), .en(Load), .reset(Reset));  // open: Qn
  D_Flip_Flop #(.trigger("falling")) d_ff_3 (
    .clk(Reloj), .D(Input[2]), .Q(SP[2]), .preset(Set), .en(Load), .reset(Reset));  // open: Qn
  D_Flip_Flop #(.trigger("falling")) d_ff_4 (
    .clk(Reloj), .D(Input[3]), .Q(SP[3]), .preset(Set), .en(Load), .reset(Reset));  // open: Qn
  D_Flip_Flop #(.trigger("falling")) d_ff_5 (
    .clk(Reloj), .D(Input[4]), .Q(SP[4]), .preset(Set), .en(Load), .reset(Reset));  // open: Qn
  D_Flip_Flop #(.trigger("falling")) d_ff_6 (
    .clk(Reloj), .D(Input[5]), .Q(SP[5]), .preset(Set), .en(Load), .reset(Reset));  // open: Qn
  D_Flip_Flop #(.trigger("falling")) d_ff_7 (
    .clk(Reloj), .D(Input[6]), .Q(SP[6]), .preset(Set), .en(Load), .reset(Reset));  // open: Qn
  D_Flip_Flop #(.trigger("falling")) d_ff_8 (
    .clk(Reloj), .D(Input[7]), .Q(SP[7]), .preset(Set), .en(Load), .reset(Reset));  // open: Qn
  D_Flip_Flop #(.trigger("falling")) d_ff_9 (
    .clk(Reloj), .D(Input[8]), .Q(SP[8]), .preset(Set), .en(Load), .reset(Reset));  // open: Qn
  D_Flip_Flop #(.trigger("falling")) d_ff_10 (
    .clk(Reloj), .D(Input[9]), .Q(SP[9]), .preset(Set), .en(Load), .reset(Reset));  // open: Qn
  D_Flip_Flop #(.trigger("falling")) d_ff_11 (
    .clk(Reloj), .D(Input[10]), .Q(SP[10]), .preset(Set), .en(Load), .reset(Reset));  // open: Qn
  D_Flip_Flop #(.trigger("falling")) d_ff_12 (
    .clk(Reloj), .D(Input[11]), .Q(SP[11]), .preset(Set), .en(Load), .reset(Reset));  // open: Qn
  D_Flip_Flop #(.trigger("falling")) d_ff_13 (
    .clk(Reloj), .D(Input[12]), .Q(SP[12]), .preset(Set), .en(Load), .reset(Reset));  // open: Qn
  D_Flip_Flop #(.trigger("falling")) d_ff_14 (
    .clk(Reloj), .D(Input[13]), .Q(SP[13]), .preset(Set), .en(Load), .reset(Reset));  // open: Qn
  D_Flip_Flop #(.trigger("falling")) d_ff_15 (
    .clk(Reloj), .D(Input[14]), .Q(SP[14]), .preset(Set), .en(Load), .reset(Reset));  // open: Qn
  D_Flip_Flop #(.trigger("falling")) d_ff_16 (
    .clk(Reloj), .D(Input[15]), .Q(SP[15]), .preset(Set), .en(Load), .reset(Reset));  // open: Qn
  D_Flip_Flop #(.trigger("falling")) d_ff_17 (
    .clk(Reloj), .D(Input[16]), .Q(SP[16]), .preset(Set), .en(Load), .reset(Reset));  // open: Qn
  D_Flip_Flop #(.trigger("falling")) d_ff_18 (
    .clk(Reloj), .D(Input[17]), .Q(SP[17]), .preset(Set), .en(Load), .reset(Reset));  // open: Qn
  D_Flip_Flop #(.trigger("falling")) d_ff_19 (
    .clk(Reloj), .D(Input[18]), .Q(SP[18]), .preset(Set), .en(Load), .reset(Reset));  // open: Qn
  D_Flip_Flop #(.trigger("falling")) d_ff_20 (
    .clk(Reloj), .D(Input[19]), .Q(SP[19]), .preset(Set), .en(Load), .reset(Reset));  // open: Qn
  D_Flip_Flop #(.trigger("falling")) d_ff_21 (
    .clk(Reloj), .D(Input[20]), .Q(SP[20]), .preset(Set), .en(Load), .reset(Reset));  // open: Qn
  D_Flip_Flop #(.trigger("falling")) d_ff_22 (
    .clk(Reloj), .D(Input[21]), .Q(SP[21]), .preset(Set), .en(Load), .reset(Reset));  // open: Qn
  D_Flip_Flop #(.trigger("falling")) d_ff_23 (
    .clk(Reloj), .D(Input[22]), .Q(SP[22]), .preset(Set), .en(Load), .reset(Reset));  // open: Qn
  D_Flip_Flop #(.trigger("falling")) d_ff_24 (
    .clk(Reloj), .D(Input[23]), .Q(SP[23]), .preset(Set), .en(Load), .reset(Reset));  // open: Qn
  D_Flip_Flop #(.trigger("falling")) d_ff_25 (
    .clk(Reloj), .D(Input[26]), .Q(SP[26]), .preset(Set), .en(Load), .reset(Reset));  // open: Qn
  D_Flip_Flop #(.trigger("falling")) d_ff_26 (
    .clk(Reloj), .D(Input[28]), .Q(SP[28]), .preset(Set), .en(Load), .reset(Reset));  // open: Qn
  D_Flip_Flop #(.trigger("falling")) d_ff_27 (
    .clk(Reloj), .D(Input[29]), .Q(SP[29]), .preset(Set), .en(Load), .reset(Reset));  // open: Qn
  D_Flip_Flop #(.trigger("falling")) d_ff_28 (
    .clk(Reloj), .D(Input[30]), .Q(SP[30]), .preset(Set), .en(Load), .reset(Reset));  // open: Qn
  D_Flip_Flop #(.trigger("falling")) d_ff_29 (
    .clk(Reloj), .D(Input[31]), .Q(SP[31]), .preset(Set), .en(Load), .reset(Reset));  // open: Qn
  D_Flip_Flop #(.trigger("falling")) d_ff_30 (
    .clk(Reloj), .D(Input[24]), .Q(SP[24]), .preset(Set), .en(Load), .reset(Reset));  // open: Qn
  D_Flip_Flop #(.trigger("falling")) d_ff_31 (
    .clk(Reloj), .D(Input[25]), .Q(SP[25]), .preset(Set), .en(Load), .reset(Reset));  // open: Qn
  D_Flip_Flop #(.trigger("falling")) d_ff_32 (
    .clk(Reloj), .D(Input[27]), .Q(SP[27]), .preset(Set), .en(Load), .reset(Reset));  // open: Qn

  // Other names for the same wires on the sheet: ClK = Reloj; Io = Input[0]; I1 = Input[1]; I2 = Input[2];
  //   I3 = Input[3]; I4 = Input[4]; I5 = Input[5]; I6 = Input[6]; I7 = Input[7]; I8 = Input[8]; I9 = Input[9];
  //   I10 = Input[10]; I11 = Input[11]; I12 = Input[12]; I13 = Input[13]; I14 = Input[14]; I15 = Input[15];
  //   I16 = Input[16]; I17 = Input[17]; I18 = Input[18]; I19 = Input[19]; I20 = Input[20]; I21 = Input[21];
  //   I22 = Input[22]; I23 = Input[23]; I24 = Input[24]; I25 = Input[25]; I26 = Input[26]; I27 = Input[27];
  //   I28 = Input[28]; I29 = Input[29]; I30 = Input[30]; I31 = Input[31]; Out_0 = SP[0]; Out_1 = SP[1]; Out_2 = SP[2];
  //   Out_3 = SP[3]; Out_4 = SP[4]; Out_5 = SP[5]; Out_6 = SP[6]; Out_7 = SP[7]; Out_8 = SP[8]; Out_9 = SP[9];
  //   Out_10 = SP[10]; Out_11 = SP[11]; Out_12 = SP[12]; Out_13 = SP[13]; Out_14 = SP[14]; Out_15 = SP[15];
  //   Out_16 = SP[16]; Out_17 = SP[17]; Out_18 = SP[18]; Out_19 = SP[19]; Out_20 = SP[20]; Out_21 = SP[21];
  //   Out_22 = SP[22]; Out_23 = SP[23]; Out_24 = SP[24]; Out_25 = SP[25]; Out_26 = SP[26]; Out_27 = SP[27];
  //   Out_28 = SP[28]; Out_29 = SP[29]; Out_30 = SP[30]; Out_31 = SP[31]
endmodule
