// Logisim project STACKPOINTER.circ as structural Verilog
module RegistroSet (
  input  Reloj,
  input  Reset,
  input  Set,
  input  Load,
  input  [31:0] Input,
  output [31:0] SP
);

  D_Flip_Flop #(.trigger("falling")) d_ff_1 (
    .clk(Reloj), .D(Input[0]), .Q(SP[0]), .preset(Set), .en(Load), .reset(Reset));  // open: Qn
  D_Flip_Flop #(.trigger("falling")) d_ff_2 (
    .clk(Reloj), .D(Input[1]), .Q(SP[1]), .preset(Set), .en(Load), .reset(Reset));  // open: Qn
  D_Flip_Flop #(.trigger("falling")) d_ff_3 (
    .clk(Reloj), .D(Input[2]), .Q(SP[2]), .preset(Set), .en(Load), .reset(Reset));  // open: Qn
  D_Flip_Flop #(.trigger("falling")) d_ff_4 (
    .clk(Reloj), .D(Input[3]), .Q(SP[3]), .preset(Set), .en(Load), .reset(Reset));  // open: Qn
  D_Flip_Flop #(.trigger("falling")) d_ff_5 (
    .clk(Reloj), .D(Input[4]), .Q(SP[4]), .preset(Set), .en(Load), .reset(Reset));  // open: Qn
  D_Flip_Flop #(.trigger("falling")) d_ff_6 (
    .clk(Reloj), .D(Input[5]), .Q(SP[5]), .preset(Set), .en(Load), .reset(Reset));  // open: Qn
  D_Flip_Flop #(.trigger("falling")) d_ff_7 (
    .clk(Reloj), .D(Input[6]), .Q(SP[6]), .preset(Set), .en(Load), .reset(Reset));  // open: Qn
  D_Flip_Flop #(.trigger("falling")) d_ff_8 (
    .clk(Reloj), .D(Input[7]), .Q(SP[7]), .preset(Set), .en(Load), .reset(Reset));  // open: Qn
  D_Flip_Flop #(.trigger("falling")) d_ff_9 (
    .clk(Reloj), .D(Input[8]), .Q(SP[8]), .preset(Set), .en(Load), .reset(Reset));  // open: Qn
  D_Flip_Flop #(.trigger("falling")) d_ff_10 (
    .clk(Reloj), .D(Input[9]), .Q(SP[9]), .preset(Set), .en(Load), .reset(Reset));  // open: Qn
  D_Flip_Flop #(.trigger("falling")) d_ff_11 (
    .clk(Reloj), .D(Input[10]), .Q(SP[10]), .preset(Set), .en(Load), .reset(Reset));  // open: Qn
  D_Flip_Flop #(.trigger("falling")) d_ff_12 (
    .clk(Reloj), .D(Input[11]), .Q(SP[11]), .preset(Set), .en(Load), .reset(Reset));  // open: Qn
  D_Flip_Flop #(.trigger("falling")) d_ff_13 (
    .clk(Reloj), .D(Input[12]), .Q(SP[12]), .preset(Set), .en(Load), .reset(Reset));  // open: Qn
  D_Flip_Flop #(.trigger("falling")) d_ff_14 (
    .clk(Reloj), .D(Input[13]), .Q(SP[13]), .preset(Set), .en(Load), .reset(Reset));  // open: Qn
  D_Flip_Flop #(.trigger("falling")) d_ff_15 (
    .clk(Reloj), .D(Input[14]), .Q(SP[14]), .preset(Set), .en(Load), .reset(Reset));  // open: Qn
  D_Flip_Flop #(.trigger("falling")) d_ff_16 (
    .clk(Reloj), .D(Input[15]), .Q(SP[15]), .preset(Set), .en(Load), .reset(Reset));  // open: Qn
  D_Flip_Flop #(.trigger("falling")) d_ff_17 (
    .clk(Reloj), .D(Input[16]), .Q(SP[16]), .preset(Set), .en(Load), .reset(Reset));  // open: Qn
  D_Flip_Flop #(.trigger("falling")) d_ff_18 (
    .clk(Reloj), .D(Input[17]), .Q(SP[17]), .preset(Set), .en(Load), .reset(Reset));  // open: Qn
  D_Flip_Flop #(.trigger("falling")) d_ff_19 (
    .clk(Reloj), .D(Input[18]), .Q(SP[18]), .preset(Set), .en(Load), .reset(Reset));  // open: Qn
  D_Flip_Flop #(.trigger("falling")) d_ff_20 (
    .clk(Reloj), .D(Input[19]), .Q(SP[19]), .preset(Set), .en(Load), .reset(Reset));  // open: Qn
  D_Flip_Flop #(.trigger("falling")) d_ff_21 (
    .clk(Reloj), .D(Input[20]), .Q(SP[20]), .preset(Set), .en(Load), .reset(Reset));  // open: Qn
  D_Flip_Flop #(.trigger("falling")) d_ff_22 (
    .clk(Reloj), .D(Input[21]), .Q(SP[21]), .preset(Set), .en(Load), .reset(Reset));  // open: Qn
  D_Flip_Flop #(.trigger("falling")) d_ff_23 (
    .clk(Reloj), .D(Input[22]), .Q(SP[22]), .preset(Set), .en(Load), .reset(Reset));  // open: Qn
  D_Flip_Flop #(.trigger("falling")) d_ff_24 (
    .clk(Reloj), .D(Input[23]), .Q(SP[23]), .preset(Set), .en(Load), .reset(Reset));  // open: Qn
  D_Flip_Flop #(.trigger("falling")) d_ff_25 (
    .clk(Reloj), .D(Input[26]), .Q(SP[26]), .preset(Set), .en(Load), .reset(Reset));  // open: Qn
  D_Flip_Flop #(.trigger("falling")) d_ff_26 (
    .clk(Reloj), .D(Input[28]), .Q(SP[28]), .preset(Set), .en(Load), .reset(Reset));  // open: Qn
  D_Flip_Flop #(.trigger("falling")) d_ff_27 (
    .clk(Reloj), .D(Input[29]), .Q(SP[29]), .preset(Set), .en(Load), .reset(Reset));  // open: Qn
  D_Flip_Flop #(.trigger("falling")) d_ff_28 (
    .clk(Reloj), .D(Input[30]), .Q(SP[30]), .preset(Set), .en(Load), .reset(Reset));  // open: Qn
  D_Flip_Flop #(.trigger("falling")) d_ff_29 (
    .clk(Reloj), .D(Input[31]), .Q(SP[31]), .preset(Set), .en(Load), .reset(Reset));  // open: Qn
  D_Flip_Flop #(.trigger("falling")) d_ff_30 (
    .clk(Reloj), .D(Input[24]), .Q(SP[24]), .preset(Set), .en(Load), .reset(Reset));  // open: Qn
  D_Flip_Flop #(.trigger("falling")) d_ff_31 (
    .clk(Reloj), .D(Input[25]), .Q(SP[25]), .preset(Set), .en(Load), .reset(Reset));  // open: Qn
  D_Flip_Flop #(.trigger("falling")) d_ff_32 (
    .clk(Reloj), .D(Input[27]), .Q(SP[27]), .preset(Set), .en(Load), .reset(Reset));  // open: Qn

  // Other names for the same wires on the sheet: ClK = Reloj; Io = Input[0]; I1 = Input[1]; I2 = Input[2];
  //   I3 = Input[3]; I4 = Input[4]; I5 = Input[5]; I6 = Input[6]; I7 = Input[7]; I8 = Input[8]; I9 = Input[9];
  //   I10 = Input[10]; I11 = Input[11]; I12 = Input[12]; I13 = Input[13]; I14 = Input[14]; I15 = Input[15];
  //   I16 = Input[16]; I17 = Input[17]; I18 = Input[18]; I19 = Input[19]; I20 = Input[20]; I21 = Input[21];
  //   I22 = Input[22]; I23 = Input[23]; I24 = Input[24]; I25 = Input[25]; I26 = Input[26]; I27 = Input[27];
  //   I28 = Input[28]; I29 = Input[29]; I30 = Input[30]; I31 = Input[31]; Out_0 = SP[0]; Out_1 = SP[1]; Out_2 = SP[2];
  //   Out_3 = SP[3]; Out_4 = SP[4]; Out_5 = SP[5]; Out_6 = SP[6]; Out_7 = SP[7]; Out_8 = SP[8]; Out_9 = SP[9];
  //   Out_10 = SP[10]; Out_11 = SP[11]; Out_12 = SP[12]; Out_13 = SP[13]; Out_14 = SP[14]; Out_15 = SP[15];
  //   Out_16 = SP[16]; Out_17 = SP[17]; Out_18 = SP[18]; Out_19 = SP[19]; Out_20 = SP[20]; Out_21 = SP[21];
  //   Out_22 = SP[22]; Out_23 = SP[23]; Out_24 = SP[24]; Out_25 = SP[25]; Out_26 = SP[26]; Out_27 = SP[27];
  //   Out_28 = SP[28]; Out_29 = SP[29]; Out_30 = SP[30]; Out_31 = SP[31]
endmodule

module STACK_POINTER (
  input  CLK,
  input  Selector_SP,
  input  in_3,
  input  in_4,
  input  in_5,
  output [31:0] out_6
);

  wire [31:0] multiplexer_1_out, SP_4, SP_4_t;

  Multiplexer #(.width(32), .enable("false")) multiplexer_1 (
    .in0(SP_4), .in1(SP_4_t), .out(multiplexer_1_out), .sel(Selector_SP));
  RegistroSet registroset_1 (.Reloj(CLK), .Reset(in_3), .Set(in_5), .Load(in_4), .Input(multiplexer_1_out), .SP(out_6));

  // Other names for the same wires on the sheet: Load__SP = in_4; OP_SP = Selector_SP; Reset = in_3; Set_SP = in_5;
  //   SP[31:0] = out_6

  // Notes on the sheet:
  //   STACK POINTER
endmodule
