// Logisim project s-mips.circ as structural Verilog
module S_MIPS_Board (
  input  DESHABILITAR_DISPATCHER,
  output halt
);

  wire button_1_out, CLK, CS, d_ff_1_q, LCLR, LoadRAM, LoadRAMOn, LW, R_R_W, R_W, ram_dispatcher_1_finished,
       RCS, Reset_out, RST, TTY_EN;
  wire [2:0] KDB;
  wire [3:0] LMask, Mask, ram_1_read_time, ram_1_write_time, RMask;
  wire [6:0] KDB_DATA, TTY_DATA;
  wire [15:0] Addr, LAddr, RAddr;
  wire [31:0] I0, I1, I2, I3, LData, ram_1_data_out_0, ram_1_data_out_1, ram_1_data_out_2, ram_1_data_out_3,
       RI0, RI1, RI2, RI3;

  TTY #(.rows(25), .cols(80)) tty_1 (.data(TTY_DATA), .clk(CLK), .we(TTY_EN), .clr(RST));
  not not_1 (LoadRAMOn, ram_dispatcher_1_finished);
  RAM_Dispatcher ram_dispatcher_1 (
    .WriteTime(ram_1_write_time), .Clock(CLK), .Data(LData), .Address(LAddr), .Mask(LMask),
    .Finished(ram_dispatcher_1_finished), .Write(LW), .CLR(LCLR));
  Keyboard #(.buflen(64)) keyboard_1 (.clk(CLK), .re(KDB[0]), .avail(KDB[2]), .data(KDB_DATA));  // open: clr
  RAM ram_1 (
    .Address(RAddr), .Data_Out_0(ram_1_data_out_0), .Data_Out_1(ram_1_data_out_1),
    .Data_Out_2(ram_1_data_out_2), .Data_Out_3(ram_1_data_out_3), .Data_In_0(RI0), .Data_In_1(RI1),
    .Data_In_2(RI2), .Data_In_3(RI3), .Mask(RMask), .nRead_Write(R_R_W), .Chip_Select(RCS),
    .Read_Time(ram_1_read_time), .Reset(button_1_out), .Write_Time(ram_1_write_time));
  Button button_1 (.out(button_1_out));
  D_Flip_Flop d_ff_1 (.clk(CLK), .D(1'b1), .Q(d_ff_1_q), .reset(Reset_out));  // open: Qn, preset, en
  Button Reset (.out(Reset_out));
  S_MIPS s_mips_1 (
    .Kbd_Enable(KDB[0]), .Address(Addr), .Kbd_Clear(KDB[1]), .Kbd_Available(KDB[2]), .RAM_In_0(I0),
    .Kbd_ASCII_Data(KDB_DATA), .RAM_In_1(I1), .TTY_Enable(TTY_EN), .RAM_In_2(I2), .RAM_In_3(I3),
    .TTY_ASCII_Data(TTY_DATA), .Reset(RST), .RAM_Out_0(ram_1_data_out_0), .Clock(CLK),
    .RAM_Out_1(ram_1_data_out_1), .Stop(halt), .RAM_Out_2(ram_1_data_out_2), .RAM_Out_3(ram_1_data_out_3),
    .Mask(Mask), .Read_Time(ram_1_read_time), .Write_Time(ram_1_write_time), .nRead_Write(R_W),
    .Chip_Select(CS));
  D_Flip_Flop d_ff_2 (.clk(CLK), .D(d_ff_1_q), .Qn(LCLR), .reset(Reset_out));  // open: Q, preset, en
  or or_1 (RST, LCLR, LoadRAM);
  Clock clock_1 (.out(CLK));
  Multiplexer #(.width(32), .enable("false")) multiplexer_1 (.in0(I0), .in1(LData), .out(RI0), .sel(LoadRAM));
  Multiplexer #(.width(32), .enable("false")) multiplexer_2 (.in0(I1), .in1(LData), .out(RI1), .sel(LoadRAM));
  Multiplexer #(.width(32), .enable("false")) multiplexer_3 (.in0(I2), .in1(LData), .out(RI2), .sel(LoadRAM));
  Multiplexer #(.width(32), .enable("false")) multiplexer_4 (.in0(I3), .in1(LData), .out(RI3), .sel(LoadRAM));
  and and_1 (LoadRAM, ~DESHABILITAR_DISPATCHER, LoadRAMOn);  // AND_Gate
  Multiplexer #(.width(16), .enable("false")) multiplexer_5 (.in0(Addr), .in1(LAddr), .out(RAddr), .sel(LoadRAM));
  Multiplexer #(.width(4), .enable("false")) multiplexer_6 (.in0(Mask), .in1(LMask), .out(RMask), .sel(LoadRAM));
  Multiplexer #(.enable("false")) multiplexer_7 (.in0(CS), .in1(LW), .out(RCS), .sel(LoadRAM));
  Multiplexer #(.enable("false")) multiplexer_8 (.in0(R_W), .in1(LW), .out(R_R_W), .sel(LoadRAM));

  // Notes on the sheet:
  //   NO MODIFICAR
  //   Keyboard
endmodule

module RAM (
  input  [15:0] Address,
  input  [31:0] Data_In_0,
  input  [31:0] Data_In_1,
  input  [31:0] Data_In_2,
  input  [31:0] Data_In_3,
  input  [3:0] Mask,
  input  nRead_Write,
  input  Chip_Select,
  input  Reset,
  output [31:0] Data_Out_0,
  output [31:0] Data_Out_1,
  output [31:0] Data_Out_2,
  output [31:0] Data_Out_3,
  output [3:0] Read_Time,
  output [3:0] Write_Time
);

  wire and_2_out, and_3_out, and_4_out, and_5_out, and_6_out, and_7_out, and_8_out, and_9_out, Changed, CLK,
       comparator_2_eq, comparator_3_eq, comparator_4_eq, comparator_5_eq, comparator_6_eq, Count,
       demultiplexer_3_out0, Idle, Idle_q, Load, Load0, Load1, nand_1_out, or_1_out, or_2_out, or_3_out,
       or_4_out, or_5_out, or_6_out, or_7_out, or_8_out, or_9_out, or_10_out, Proc_q, Update_Mem, Zero_Time;
  wire [3:0] counter_1_q, multiplexer_1_out, subtractor_1_out;
  wire [31:0] register_1_q, register_2_q, register_3_q, register_4_q, register_5_q;

  // Probe on 4'b0011
  // Probe on 4'b0010
  Multiplexer #(.width(4), .enable("false")) multiplexer_1 (
    .in0(4'b0011), .in1(4'b0010), .out(multiplexer_1_out), .sel(nRead_Write));
  or or_1 (or_1_out, Idle, Update_Mem);
  or or_2 (or_2_out, ~Chip_Select, Reset);  // OR_Gate
  Subtractor #(.width(4)) subtractor_1 (.a(multiplexer_1_out), .b(4'b0010), .out(subtractor_1_out));  // open: bin, bout
  Demultiplexer #(.enable("false")) demultiplexer_1 (.out0(Idle), .out1(Load0), .in(Idle_q), .sel(Changed));
  D_Flip_Flop u_Idle (.clk(CLK), .D(or_1_out), .Q(Idle_q), .preset(or_2_out));  // open: Qn, en, reset
  // Probe on counter_1_q
  Counter #(.width(4), .max('hf)) counter_1 (
    .load(Load), .D(subtractor_1_out), .count(Count), .Q(counter_1_q), .clk(CLK), .clr(or_3_out));  // open: carry
  or or_3 (or_3_out, ~Chip_Select, Reset);  // OR_Gate
  Comparator #(.width(4), .mode("unsigned")) comparator_1 (
    .a(4'b0000), .b(counter_1_q), .eq(Zero_Time));  // open: gt, lt
  or or_4 (or_4_out, Count, Load0, Load1);
  Register #(.width(32)) register_1 (.D(Data_In_0), .en(Chip_Select), .Q(register_1_q), .clk(CLK), .clr(or_5_out));
  or or_5 (or_5_out, ~Chip_Select, Reset);  // OR_Gate
  Register #(.width(32)) register_2 (.D(Data_In_1), .en(Chip_Select), .Q(register_2_q), .clk(CLK), .clr(or_6_out));
  or or_6 (or_6_out, ~Chip_Select, Reset);  // OR_Gate
  Register #(.width(32)) register_3 (.D(Data_In_2), .en(Chip_Select), .Q(register_3_q), .clk(CLK), .clr(or_7_out));
  or or_7 (or_7_out, ~Chip_Select, Reset);  // OR_Gate
  Register #(.width(32)) register_4 (.D(Data_In_3), .en(Chip_Select), .Q(register_4_q), .clk(CLK), .clr(or_8_out));
  or or_8 (or_8_out, ~Chip_Select, Reset);  // OR_Gate
  Register #(.width(32)) register_5 (
    .D({{11{1'b1}}, nRead_Write, Mask, Address}), .en(Chip_Select), .Q(register_5_q), .clk(CLK),
    .clr(or_9_out));
  or or_9 (or_9_out, ~Chip_Select, Reset);  // OR_Gate
  D_Flip_Flop Proc (.clk(CLK), .D(or_4_out), .Q(Proc_q), .reset(or_10_out));  // open: Qn, preset, en
  or or_10 (or_10_out, ~Chip_Select, Reset);  // OR_Gate
  Demultiplexer #(.enable("false")) demultiplexer_2 (
    .out0(Count), .out1(Update_Mem), .in(demultiplexer_3_out0), .sel(Zero_Time));
  Demultiplexer #(.enable("false")) demultiplexer_3 (
    .out0(demultiplexer_3_out0), .out1(Load1), .in(Proc_q), .sel(Changed));
  Clock clock_1 (.out(CLK));
  Comparator #(.width(32)) comparator_2 (.a(register_1_q), .b(Data_In_0), .eq(comparator_2_eq));  // open: gt, lt
  Comparator #(.width(32)) comparator_3 (.a(register_2_q), .b(Data_In_1), .eq(comparator_3_eq));  // open: gt, lt
  Comparator #(.width(32)) comparator_4 (.a(register_3_q), .b(Data_In_2), .eq(comparator_4_eq));  // open: gt, lt
  Comparator #(.width(32)) comparator_5 (.a(register_4_q), .b(Data_In_3), .eq(comparator_5_eq));  // open: gt, lt
  Comparator #(.width(32)) comparator_6 (
    .a(register_5_q), .b({{11{1'b1}}, nRead_Write, Mask, Address}), .eq(comparator_6_eq));  // open: gt, lt
  nand nand_1 (nand_1_out, comparator_6_eq, comparator_2_eq, comparator_3_eq, comparator_4_eq, comparator_5_eq);
  and and_1 (Changed, nand_1_out, Chip_Select);
  or or_11 (Load, Count, Load1, Load0);
  and and_2 (and_2_out, Mask[0], Update_Mem, nRead_Write);
  and and_3 (and_3_out, Mask[1], Update_Mem, nRead_Write);
  and and_4 (and_4_out, Mask[2], Update_Mem, nRead_Write);
  and and_5 (and_5_out, Mask[3], Update_Mem, nRead_Write);
  RAM_part #(.addrWidth(16), .dataWidth(32), .bus("separate")) ram_1 (
    .addr(Address), .din(Data_In_0), .data(Data_Out_0), .str(and_2_out), .sel(Chip_Select), .clk(CLK),
    .ld(and_6_out), .clr(Reset));
  and and_6 (and_6_out, ~nRead_Write, Idle);  // AND_Gate
  RAM_part #(.addrWidth(16), .dataWidth(32), .bus("separate")) ram_2 (
    .addr(Address), .din(Data_In_1), .data(Data_Out_1), .str(and_3_out), .sel(Chip_Select), .clk(CLK),
    .ld(and_7_out), .clr(Reset));
  and and_7 (and_7_out, ~nRead_Write, Idle);  // AND_Gate
  RAM_part #(.addrWidth(16), .dataWidth(32), .bus("separate")) ram_3 (
    .addr(Address), .din(Data_In_2), .data(Data_Out_2), .str(and_4_out), .sel(Chip_Select), .clk(CLK),
    .ld(and_8_out), .clr(Reset));
  and and_8 (and_8_out, ~nRead_Write, Idle);  // AND_Gate
  RAM_part #(.addrWidth(16), .dataWidth(32), .bus("separate")) ram_4 (
    .addr(Address), .din(Data_In_3), .data(Data_Out_3), .str(and_5_out), .sel(Chip_Select), .clk(CLK),
    .ld(and_9_out), .clr(Reset));
  and and_9 (and_9_out, ~nRead_Write, Idle);  // AND_Gate

  assign Read_Time = 4'b0011;
  assign Write_Time = 4'b0010;

  // Other names for the same wires on the sheet: M0 = Mask[0]; M1 = Mask[1]; M2 = Mask[2]; M3 = Mask[3];
  //   RW = nRead_Write; CLR = Reset; CS = Chip_Select; Load2 = Count

  // Notes on the sheet:
  //   NO MODIFICAR
  //   excepto quizás los valores RT y WT
  //   BANK0
  //   BANK1
  //   BANK2
  //   BANK3
endmodule

module S_MIPS (
  input  Kbd_Available,
  input  [31:0] RAM_Out_0,
  input  [6:0] Kbd_ASCII_Data,
  input  [31:0] RAM_Out_1,
  input  [31:0] RAM_Out_2,
  input  Reset,
  input  Clock,
  input  [31:0] RAM_Out_3,
  input  [3:0] Read_Time,
  input  [3:0] Write_Time,
  output Kbd_Enable,
  output Kbd_Clear,
  output [31:0] RAM_In_0,
  output [3:0] Mask,
  output [31:0] RAM_In_1,
  output nRead_Write,
  output TTY_Enable,
  output Chip_Select,
  output [6:0] TTY_ASCII_Data,
  output [31:0] RAM_In_2,
  output [31:0] RAM_In_3,
  output Stop,
  output [15:0] Address
);

  wire control_unit_1_load_program_counter, control_unit_1_load_register_file, control_unit_1_loadsp,
       CScache, demultiplexer_1_out0, demultiplexer_1_out1, demultiplexer_1_out2, demultiplexer_1_out3,
       FINISH, HALT, LA, LI, not_1_out, RO, RWCACHE, SorP;
  wire [1:0] OFFSET, SELECT_ADRESS;
  wire [3:0] CU_OP;
  wire [31:0] cache_unit_1_out_22, cache_unit_1_out_25, DM, I1, I2, I3, I4, MA, multiplexer_1_out, O1, O2,
       O3, O4, PC, RO1, RO2, RO3, RO4, SP;

  not not_1 (not_1_out, Stop);
  INVERTER inverter_1 (
    .RAM_OUT1(RAM_Out_0), .RAM_OUT2(RAM_Out_1), .RAM_OUT3(RAM_Out_2), .RAM_OUT4(RAM_Out_3), .out_5(RO1),
    .out_6(RO2), .out_7(RO3), .out_8(RO4));
  Multiplexer #(.select(2), .width(32), .enable("false")) multiplexer_1 (
    .in0(PC), .in1(SP), .in2(MA), .out({multiplexer_1_out[31:4], OFFSET, multiplexer_1_out[1:0]}),
    .sel(SELECT_ADRESS));  // open: in3
  CACHE_UNIT cache_unit_1 (
    .in_1(not_1_out), .RST(Reset), .in_3(Clock), .rw(RWCACHE), .in_7(CScache), .in_8(RO), .in_11(O1),
    .in_13(O2), .in_14(O3), .in_15(O4), .FINISH(FINISH), .CST(Chip_Select), .out_18(I1), .RAMADRESS(Address),
    .out_20(I2), .RW_RAM(nRead_Write), .out_22(cache_unit_1_out_22), .out_23(I3), .out_24(I4),
    .out_25(cache_unit_1_out_25), .in_6(Write_Time), .in_5(Read_Time),
    .ADRESS({multiplexer_1_out[31:4], OFFSET, multiplexer_1_out[1:0]}), .LOADADRESS(LA), .in_12(LI));
  Demultiplexer #(.select(2), .enable("false")) demultiplexer_1 (
    .out0(demultiplexer_1_out0), .out1(demultiplexer_1_out1), .out2(demultiplexer_1_out2),
    .out3(demultiplexer_1_out3), .in(SorP), .sel(OFFSET));
  INVERTER inverter_2 (
    .RAM_OUT1(I1), .RAM_OUT2(I2), .RAM_OUT3(I3), .RAM_OUT4(I4), .out_5(RAM_In_0), .out_6(RAM_In_1),
    .out_7(RAM_In_2), .out_8(RAM_In_3));
  Multiplexer #(.width(32), .enable("false")) multiplexer_2 (.in0(RO1), .in1(DM), .out(O1), .sel(demultiplexer_1_out0));
  Multiplexer #(.width(32), .enable("false")) multiplexer_3 (.in0(RO2), .in1(DM), .out(O2), .sel(demultiplexer_1_out1));
  Multiplexer #(.width(32), .enable("false")) multiplexer_4 (.in0(RO3), .in1(DM), .out(O3), .sel(demultiplexer_1_out2));
  Multiplexer #(.width(32), .enable("false")) multiplexer_5 (.in0(RO4), .in1(DM), .out(O4), .sel(demultiplexer_1_out3));
  Control_Unit control_unit_1 (
    .Reset(Reset), .operacion(CU_OP), .Wait(FINISH), .Load_Register_File(control_unit_1_load_register_file),
    .Escribir_RAM(RWCACHE), .RAM_Control(CScache), .KBD_ENABLE(Kbd_Enable),
    .Load_Program_Counter(control_unit_1_load_program_counter), .LoadMemory(LA),
    .LOADSP(control_unit_1_loadsp), .Reloj(Clock), .TTY_ENABLE(TTY_Enable), .\end (Stop), .out_16(LI),
    .out_15(RO));  // open: in_5
  DATAPATH datapath_1 (
    .in_1(cache_unit_1_out_22), .CLK(Clock), .RESET(Reset), .in_4(Kbd_ASCII_Data), .in_5(Kbd_Available),
    .DATO_MEMORIA(cache_unit_1_out_25), .in_7(control_unit_1_load_register_file),
    .LOAD_PC(control_unit_1_load_program_counter), .TTYDATA(TTY_ASCII_Data), .CU_OP(CU_OP), .PC(PC),
    .Stack_Pointer(SP), .MEMORYADRESS(MA), .SELECTADRESS(SELECT_ADRESS), .in_8(control_unit_1_loadsp),
    .STOP(HALT), .DATAMEMORYOUT(DM), .PUSH_OR_SW(SorP));

  assign Kbd_Clear = Reset;
  assign Mask = 4'b1111;

  // Other names for the same wires on the sheet: CLK = Clock; CS = Chip_Select; KBD_AVAIL = Kbd_Available;
  //   CLR = Reset; KBD_CLR = Reset; KBD_DATA[6:0] = Kbd_ASCII_Data; RAM_A[15:0] = Address;
  //   RAM_INPUT_0[31:0] = RAM_In_0; RAM_INPUT_1[31:0] = RAM_In_1; RAM_INPUT_2[31:0] = RAM_In_2;
  //   RAM_INPUT_3[31:0] = RAM_In_3; RAM_OUTPUT_0[31:0] = RAM_Out_0; RAM_OUTPUT_1[31:0] = RAM_Out_1;
  //   RAM_OUTPUT_2[31:0] = RAM_Out_2; RAM_OUTPUT_3[31:0] = RAM_Out_3; RW = nRead_Write;
  //   TTY_DATA[6:0] = TTY_ASCII_Data

  // Notes on the sheet:
  //   INPUTS
  //   DATA FROM RAM
  //   RAM TIMING
  //   RAM CONTROL
  //   RAM ADDRESS
  //   DATA WRITE MASK
  //   OUTPUTS-RAM
  //   DATA TO RAM
  //   KEYBOARD
  //   TTY
  //   SEQUENCING
endmodule

module RAM_Dispatcher (
  input  [3:0] WriteTime,
  input  Clock,
  input  CLR,
  output [31:0] Data,
  output [15:0] Address,
  output [3:0] Mask,
  output Finished,
  output Write
);

  wire demultiplexer_2_out1, demultiplexer_3_out1, End, IDLE_q, IncAddr, Load, or_1_out, or_2_out, While_q,
       WriteEnd;
  wire [3:0] counter_1_q;
  wire [31:0] CurrentAddress_q;

  Counter #(.width(32), .max('hffffffff)) CurrentAddress (
    .count(IncAddr), .Q({CurrentAddress_q[31:18], Address, CurrentAddress_q[1:0]}), .clk(Clock), .clr(CLR));  // open: load, D, carry
  or or_1 (or_1_out, IncAddr, demultiplexer_3_out1, Finished);
  D_Flip_Flop IDLE (.clk(Clock), .D(or_1_out), .Q(IDLE_q), .preset(CLR));  // open: Qn, en, reset
  Demultiplexer #(.enable("false")) demultiplexer_1 (.out0(Load), .out1(Finished), .in(IDLE_q), .sel(End));
  D_Flip_Flop While (.clk(Clock), .D(or_2_out), .Q(While_q), .reset(CLR));  // open: Qn, preset, en
  or or_2 (or_2_out, Write, Load);
  RAM_part #(.addrWidth(18), .dataWidth(32)) ram_1 (
    .addr({Address, CurrentAddress_q[1:0]}), .data(Data), .clk(Clock));  // open: sel, ld, clr
  Demultiplexer #(.enable("false")) demultiplexer_2 (
    .out0(Write), .out1(demultiplexer_2_out1), .in(While_q), .sel(WriteEnd));
  Decoder #(.select(2)) decoder_1 (
    .out0(Mask[0]), .out1(Mask[1]), .out2(Mask[2]), .out3(Mask[3]), .sel(CurrentAddress_q[1:0]));  // open: en
  Demultiplexer #(.enable("false")) demultiplexer_3 (
    .out0(IncAddr), .out1(demultiplexer_3_out1), .in(demultiplexer_2_out1), .sel(End));
  Counter #(.width(4), .max('hf)) counter_1 (
    .load(Load), .D(WriteTime), .count(Write), .Q(counter_1_q), .clk(Clock));  // open: carry, clr
  Comparator #(.width(32)) comparator_1 (.a(Data), .b({32{1'b1}}), .eq(End));  // open: gt, lt
  Comparator #(.width(4)) comparator_2 (.a(4'b0000), .b(counter_1_q), .eq(WriteEnd));  // open: gt, lt

  // Other names for the same wires on the sheet: CLK = Clock; Count = Write; WT[3:0] = WriteTime
endmodule

module DATAPATH (
  input  [31:0] in_1,
  input  CLK,
  input  RESET,
  input  [6:0] in_4,
  input  in_5,
  input  [31:0] DATO_MEMORIA,
  input  in_7,
  input  in_8,
  input  LOAD_PC,
  output STOP,
  output [6:0] TTYDATA,
  output [3:0] CU_OP,
  output [31:0] PC,
  output [31:0] Stack_Pointer,
  output [31:0] MEMORYADRESS,
  output [31:0] DATAMEMORYOUT,
  output PUSH_OR_SW,
  output [1:0] SELECTADRESS
);

  wire and_3_out, HILO, PUSH, Selector_DA, Selector_SP, SW;
  wire [1:0] Selector_B, Selector_BC;
  wire [2:0] SELECTOR_DATAIN;
  wire [3:0] Alu_OP;
  wire [4:0] DA, RD, RS, RT;
  wire [5:0] Function, OPCode;
  wire [15:0] OFFSET;
  wire [25:0] Destino;
  wire [31:0] adder_1_out, ALU_OUT, bit_extender_1_out, bit_extender_2_out, bit_extender_3_out,
       bit_extender_4_out, branch_control_1_pc, DataIN, DataSP, HI, HIRF, LO, LORF, multiplexer_1_out,
       multiplexer_7_out, multiplexer_8_out, OFFSETEXTend, random_1_out, RT_t, subtractor_1_out;
  wire [31:7] RS_t;

  Random #(.width(32), .seed(212)) random_1 (.clk(CLK), .next(1'b1), .out(random_1_out), .clr(RESET));
  InstructionDec instructiondec_1 (
    .Instruccion(in_1), .Function(Function), .Rd(RD), .Rt(RT), .Rs(RS), .Offset(OFFSET), .Destino(Destino),
    .OP_Code(OPCode), .in_3(CLK), .in_2(RESET));  // open: Shamt
  Multiplexer #(.width(32), .enable("false")) multiplexer_1 (
    .in0({32{1'b1}}), .in1(bit_extender_1_out), .out(multiplexer_1_out), .sel(in_5));
  assign bit_extender_1_out = {{25{1'b0}}, in_4};  // Bit_Extender bit_extender_1
  and and_1 (SW, CU_OP[0], ~CU_OP[1], ~CU_OP[2], CU_OP[3]);  // AND_Gate
  and and_2 (PUSH, CU_OP[0], CU_OP[1], CU_OP[2], ~CU_OP[3]);  // AND_Gate
  Multiplexer #(.select(3), .width(32), .enable("false")) multiplexer_2 (
    .in0(ALU_OUT), .in1(HIRF), .in2(LORF), .in3(DATO_MEMORIA), .in4(DATO_MEMORIA), .in5(random_1_out),
    .in6(multiplexer_1_out), .out(DataIN), .sel(SELECTOR_DATAIN));  // open: in7
  Multiplexer #(.width(5), .enable("false")) multiplexer_3 (.in0(RD), .in1(RT), .out(DA), .sel(Selector_DA));
  Adder #(.width(32)) adder_1 (.a(Stack_Pointer), .b(32'h4), .out(adder_1_out));  // open: cin, cout
  Subtractor #(.width(32)) subtractor_1 (.a(Stack_Pointer), .b(32'h4), .out(subtractor_1_out));  // open: bin, bout
  Multiplexer #(.width(32), .enable("false")) multiplexer_4 (
    .in0(adder_1_out), .in1(subtractor_1_out), .out(DataSP), .sel(Selector_SP));
  Multiplexer #(.width(32), .enable("false")) multiplexer_5 (
    .in0({RS_t, TTYDATA}), .in1(RT_t), .out(DATAMEMORYOUT), .sel(SW));
  or or_1 (PUSH_OR_SW, PUSH, SW);
  assign bit_extender_2_out = {{16{1'b0}}, OFFSET};  // Bit_Extender bit_extender_2
  assign bit_extender_3_out = {{16{OFFSET[15]}}, OFFSET};  // Bit_Extender bit_extender_3
  Multiplexer #(.width(32), .enable("false")) multiplexer_6 (
    .in0(bit_extender_2_out), .in1(bit_extender_3_out), .out(OFFSETEXTend), .sel(OFFSET[15]));
  assign bit_extender_4_out = {{6{1'b0}}, Destino};  // Bit_Extender bit_extender_4
  Operation_Decoder operation_decoder_1 (
    .INFO__RS({RS_t, TTYDATA}), .INFO__RT(RT_t), .Selector_BC(Selector_BC), .ALU_OP(Alu_OP), .CU_OP(CU_OP),
    .in_1(OPCode), .in_2(Function), .SelectorDA(Selector_DA), .SelectorDataIN(SELECTOR_DATAIN),
    .SelectorB(Selector_B), .SelectorSP(Selector_SP), .SELECTADRESS(SELECTADRESS), .HILO(HILO), .HALT(STOP));
  Multiplexer #(.width(32), .enable("false")) multiplexer_7 (
    .in0(OFFSETEXTend), .in1(bit_extender_4_out), .out(multiplexer_7_out), .sel(and_3_out));
  and and_3 (and_3_out, Selector_BC[1], ~Selector_BC[0]);  // AND_Gate
  Register_File register_file_1 (
    .Reloj(CLK), .Reset(RESET), .RW(in_7), .DI(DataIN), .DA(DA), .SA(RS), .SB(RT), .Mult_or_Div(HILO),
    .HI(HI), .Lo(LO), .Output_Hi(HIRF), .Output_Lo(LORF), .Output_A({RS_t, TTYDATA}), .Output__B(RT_t),
    .SP(DataSP), .SP_2(Stack_Pointer), .in_5(in_8));
  Branch_Control branch_control_1 (
    .in_1(PC), .in_2(multiplexer_7_out), .in_3({RS_t, TTYDATA}), .Operacion(Selector_BC),
    .PC(branch_control_1_pc));
  Multiplexer #(.select(2), .width(32), .enable("false")) multiplexer_8 (
    .in0(RT_t), .in1(OFFSETEXTend), .out(multiplexer_8_out), .sel(Selector_B));  // open: in2, in3
  Program_Counter program_counter_1 (.PC(branch_control_1_pc), .Load(LOAD_PC), .Reset(RESET), .Reloj(CLK), .in_2(PC));
  Adder #(.width(32)) adder_2 (
    .a({RS_t, TTYDATA}), .b({{17{OFFSET[15]}}, OFFSET[14:0]}), .out(MEMORYADRESS));  // open: cin, cout
  ALU alu_1 (
    .A({RS_t, TTYDATA}), .in_2(Alu_OP), .B(multiplexer_8_out), .Out(ALU_OUT), .Hi(HI), .Lo(LO));  // open: Zero, Negativo, A_B, Equals

  // Other names for the same wires on the sheet: CUOP[3:0] = CU_OP; KBD_AVIABLE = in_5; KBD_DATA[6:0] = in_4;
  //   LPC = LOAD_PC; LSP = in_8; M___Rs_______I15__16______I15_0[31:0] = DATO_MEMORIA; M__SP[31:0] = DATO_MEMORIA;
  //   RS_t[6:0] = TTYDATA; RW_RF = in_7; SP[31:0] = Stack_Pointer

  // Notes on the sheet:
  //   in_1: pull=down
  //   in_4: pull=down
  //   INSTRUCCION
  //   SELECTORES Y LOADS
  //   DATA-IN
  //   STACK POINTER
  //   REGISTER FILE 
  //   BRANCH CONTROL
  //   PC
endmodule
